// Logisim project s-mips.circ as structural Verilog: 30 circuits, main circuit S-MIPS Board
module S_MIPS_Board (
  input  DESHABILITAR_DISPATCHER,
  output halt
);

  wire button_1_out, CLK, CS, d_ff_1_q, LCLR, LoadRAM, LoadRAMOn, LW, R_R_W, R_W, ram_dispatcher_1_finished,
       RCS, Reset_out, RST, TTY_EN;
  wire [2:0] KDB;
  wire [3:0] LMask, Mask, ram_1_read_time, ram_1_write_time, RMask;
  wire [6:0] KDB_DATA, TTY_DATA;
  wire [15:0] Addr, LAddr, RAddr;
  wire [31:0] I0, I1, I2, I3, LData, ram_1_data_out_0, ram_1_data_out_1, ram_1_data_out_2, ram_1_data_out_3,
       RI0, RI1, RI2, RI3;

  TTY #(.rows(25), .cols(80)) tty_1 (.data(TTY_DATA), .clk(CLK), .we(TTY_EN), .clr(RST));
  not not_1 (LoadRAMOn, ram_dispatcher_1_finished);
  RAM_Dispatcher ram_dispatcher_1 (
    .WriteTime(ram_1_write_time), .Clock(CLK), .Data(LData), .Address(LAddr), .Mask(LMask),
    .Finished(ram_dispatcher_1_finished), .Write(LW), .CLR(LCLR));
  Keyboard #(.buflen(64)) keyboard_1 (.clk(CLK), .re(KDB[0]), .avail(KDB[2]), .data(KDB_DATA));  // open: clr
  RAM ram_1 (
    .Address(RAddr), .Data_Out_0(ram_1_data_out_0), .Data_Out_1(ram_1_data_out_1),
    .Data_Out_2(ram_1_data_out_2), .Data_Out_3(ram_1_data_out_3), .Data_In_0(RI0), .Data_In_1(RI1),
    .Data_In_2(RI2), .Data_In_3(RI3), .Mask(RMask), .nRead_Write(R_R_W), .Chip_Select(RCS),
    .Read_Time(ram_1_read_time), .Reset(button_1_out), .Write_Time(ram_1_write_time));
  Button button_1 (.out(button_1_out));
  D_Flip_Flop d_ff_1 (.clk(CLK), .D(1'b1), .Q(d_ff_1_q), .reset(Reset_out));  // open: Qn, preset, en
  Button Reset (.out(Reset_out));
  S_MIPS s_mips_1 (
    .Kbd_Enable(KDB[0]), .Address(Addr), .Kbd_Clear(KDB[1]), .Kbd_Available(KDB[2]), .RAM_In_0(I0),
    .Kbd_ASCII_Data(KDB_DATA), .RAM_In_1(I1), .TTY_Enable(TTY_EN), .RAM_In_2(I2), .RAM_In_3(I3),
    .TTY_ASCII_Data(TTY_DATA), .Reset(RST), .RAM_Out_0(ram_1_data_out_0), .Clock(CLK),
    .RAM_Out_1(ram_1_data_out_1), .Stop(halt), .RAM_Out_2(ram_1_data_out_2), .RAM_Out_3(ram_1_data_out_3),
    .Mask(Mask), .Read_Time(ram_1_read_time), .Write_Time(ram_1_write_time), .nRead_Write(R_W),
    .Chip_Select(CS));
  D_Flip_Flop d_ff_2 (.clk(CLK), .D(d_ff_1_q), .Qn(LCLR), .reset(Reset_out));  // open: Q, preset, en
  or or_1 (RST, LCLR, LoadRAM);
  Clock clock_1 (.out(CLK));
  Multiplexer #(.width(32), .enable("false")) multiplexer_1 (.in0(I0), .in1(LData), .out(RI0), .sel(LoadRAM));
  Multiplexer #(.width(32), .enable("false")) multiplexer_2 (.in0(I1), .in1(LData), .out(RI1), .sel(LoadRAM));
  Multiplexer #(.width(32), .enable("false")) multiplexer_3 (.in0(I2), .in1(LData), .out(RI2), .sel(LoadRAM));
  Multiplexer #(.width(32), .enable("false")) multiplexer_4 (.in0(I3), .in1(LData), .out(RI3), .sel(LoadRAM));
  and and_1 (LoadRAM, ~DESHABILITAR_DISPATCHER, LoadRAMOn);  // AND_Gate
  Multiplexer #(.width(16), .enable("false")) multiplexer_5 (.in0(Addr), .in1(LAddr), .out(RAddr), .sel(LoadRAM));
  Multiplexer #(.width(4), .enable("false")) multiplexer_6 (.in0(Mask), .in1(LMask), .out(RMask), .sel(LoadRAM));
  Multiplexer #(.enable("false")) multiplexer_7 (.in0(CS), .in1(LW), .out(RCS), .sel(LoadRAM));
  Multiplexer #(.enable("false")) multiplexer_8 (.in0(R_W), .in1(LW), .out(R_R_W), .sel(LoadRAM));

  // Notes on the sheet:
  //   NO MODIFICAR
  //   Keyboard
endmodule

module RAM (
  input  [15:0] Address,
  input  [31:0] Data_In_0,
  input  [31:0] Data_In_1,
  input  [31:0] Data_In_2,
  input  [31:0] Data_In_3,
  input  [3:0] Mask,
  input  nRead_Write,
  input  Chip_Select,
  input  Reset,
  output [31:0] Data_Out_0,
  output [31:0] Data_Out_1,
  output [31:0] Data_Out_2,
  output [31:0] Data_Out_3,
  output [3:0] Read_Time,
  output [3:0] Write_Time
);

  wire and_2_out, and_3_out, and_4_out, and_5_out, and_6_out, and_7_out, and_8_out, and_9_out, Changed, CLK,
       comparator_2_eq, comparator_3_eq, comparator_4_eq, comparator_5_eq, comparator_6_eq, Count,
       demultiplexer_3_out0, Idle, Idle_q, Load, Load0, Load1, nand_1_out, or_1_out, or_2_out, or_3_out,
       or_4_out, or_5_out, or_6_out, or_7_out, or_8_out, or_9_out, or_10_out, Proc_q, Update_Mem, Zero_Time;
  wire [3:0] counter_1_q, multiplexer_1_out, subtractor_1_out;
  wire [31:0] register_1_q, register_2_q, register_3_q, register_4_q, register_5_q;

  // Probe on 4'b0011
  // Probe on 4'b0010
  Multiplexer #(.width(4), .enable("false")) multiplexer_1 (
    .in0(4'b0011), .in1(4'b0010), .out(multiplexer_1_out), .sel(nRead_Write));
  or or_1 (or_1_out, Idle, Update_Mem);
  or or_2 (or_2_out, ~Chip_Select, Reset);  // OR_Gate
  Subtractor #(.width(4)) subtractor_1 (.a(multiplexer_1_out), .b(4'b0010), .out(subtractor_1_out));  // open: bin, bout
  D_Flip_Flop u_Idle (.clk(CLK), .D(or_1_out), .Q(Idle_q), .preset(or_2_out));  // open: Qn, en, reset
  Demultiplexer #(.enable("false")) demultiplexer_1 (.out0(Idle), .out1(Load0), .in(Idle_q), .sel(Changed));
  // Probe on counter_1_q
  Counter #(.width(4), .max('hf)) counter_1 (
    .load(Load), .D(subtractor_1_out), .count(Count), .Q(counter_1_q), .clk(CLK), .clr(or_3_out));  // open: carry
  or or_3 (or_3_out, ~Chip_Select, Reset);  // OR_Gate
  Comparator #(.width(4), .mode("unsigned")) comparator_1 (
    .a(4'b0000), .b(counter_1_q), .eq(Zero_Time));  // open: gt, lt
  or or_4 (or_4_out, Count, Load0, Load1);
  Register #(.width(32)) register_1 (.D(Data_In_0), .en(Chip_Select), .Q(register_1_q), .clk(CLK), .clr(or_5_out));
  or or_5 (or_5_out, ~Chip_Select, Reset);  // OR_Gate
  Register #(.width(32)) register_2 (.D(Data_In_1), .en(Chip_Select), .Q(register_2_q), .clk(CLK), .clr(or_6_out));
  or or_6 (or_6_out, ~Chip_Select, Reset);  // OR_Gate
  Register #(.width(32)) register_3 (.D(Data_In_2), .en(Chip_Select), .Q(register_3_q), .clk(CLK), .clr(or_7_out));
  or or_7 (or_7_out, ~Chip_Select, Reset);  // OR_Gate
  Register #(.width(32)) register_4 (.D(Data_In_3), .en(Chip_Select), .Q(register_4_q), .clk(CLK), .clr(or_8_out));
  or or_8 (or_8_out, ~Chip_Select, Reset);  // OR_Gate
  Register #(.width(32)) register_5 (
    .D({{11{1'b1}}, nRead_Write, Mask, Address}), .en(Chip_Select), .Q(register_5_q), .clk(CLK),
    .clr(or_9_out));
  or or_9 (or_9_out, ~Chip_Select, Reset);  // OR_Gate
  D_Flip_Flop Proc (.clk(CLK), .D(or_4_out), .Q(Proc_q), .reset(or_10_out));  // open: Qn, preset, en
  or or_10 (or_10_out, ~Chip_Select, Reset);  // OR_Gate
  Demultiplexer #(.enable("false")) demultiplexer_2 (
    .out0(Count), .out1(Update_Mem), .in(demultiplexer_3_out0), .sel(Zero_Time));
  Demultiplexer #(.enable("false")) demultiplexer_3 (
    .out0(demultiplexer_3_out0), .out1(Load1), .in(Proc_q), .sel(Changed));
  Clock clock_1 (.out(CLK));
  Comparator #(.width(32)) comparator_2 (.a(register_1_q), .b(Data_In_0), .eq(comparator_2_eq));  // open: gt, lt
  Comparator #(.width(32)) comparator_3 (.a(register_2_q), .b(Data_In_1), .eq(comparator_3_eq));  // open: gt, lt
  Comparator #(.width(32)) comparator_4 (.a(register_3_q), .b(Data_In_2), .eq(comparator_4_eq));  // open: gt, lt
  Comparator #(.width(32)) comparator_5 (.a(register_4_q), .b(Data_In_3), .eq(comparator_5_eq));  // open: gt, lt
  Comparator #(.width(32)) comparator_6 (
    .a(register_5_q), .b({{11{1'b1}}, nRead_Write, Mask, Address}), .eq(comparator_6_eq));  // open: gt, lt
  nand nand_1 (nand_1_out, comparator_6_eq, comparator_2_eq, comparator_3_eq, comparator_4_eq, comparator_5_eq);
  and and_1 (Changed, nand_1_out, Chip_Select);
  or or_11 (Load, Count, Load1, Load0);
  and and_2 (and_2_out, Mask[0], Update_Mem, nRead_Write);
  and and_3 (and_3_out, Mask[1], Update_Mem, nRead_Write);
  and and_4 (and_4_out, Mask[2], Update_Mem, nRead_Write);
  and and_5 (and_5_out, Mask[3], Update_Mem, nRead_Write);
  RAM_part #(.addrWidth(16), .dataWidth(32), .bus("separate")) ram_1 (
    .addr(Address), .din(Data_In_0), .data(Data_Out_0), .str(and_2_out), .sel(Chip_Select), .clk(CLK),
    .ld(and_6_out), .clr(Reset));
  and and_6 (and_6_out, ~nRead_Write, Idle);  // AND_Gate
  RAM_part #(.addrWidth(16), .dataWidth(32), .bus("separate")) ram_2 (
    .addr(Address), .din(Data_In_1), .data(Data_Out_1), .str(and_3_out), .sel(Chip_Select), .clk(CLK),
    .ld(and_7_out), .clr(Reset));
  and and_7 (and_7_out, ~nRead_Write, Idle);  // AND_Gate
  RAM_part #(.addrWidth(16), .dataWidth(32), .bus("separate")) ram_3 (
    .addr(Address), .din(Data_In_2), .data(Data_Out_2), .str(and_4_out), .sel(Chip_Select), .clk(CLK),
    .ld(and_8_out), .clr(Reset));
  and and_8 (and_8_out, ~nRead_Write, Idle);  // AND_Gate
  RAM_part #(.addrWidth(16), .dataWidth(32), .bus("separate")) ram_4 (
    .addr(Address), .din(Data_In_3), .data(Data_Out_3), .str(and_5_out), .sel(Chip_Select), .clk(CLK),
    .ld(and_9_out), .clr(Reset));
  and and_9 (and_9_out, ~nRead_Write, Idle);  // AND_Gate

  assign Read_Time = 4'b0011;
  assign Write_Time = 4'b0010;

  // Other names for the same wires on the sheet: M0 = Mask[0]; M1 = Mask[1]; M2 = Mask[2]; M3 = Mask[3];
  //   RW = nRead_Write; CLR = Reset; CS = Chip_Select; Load2 = Count

  // Notes on the sheet:
  //   NO MODIFICAR
  //   excepto quizás los valores RT y WT
  //   BANK0
  //   BANK1
  //   BANK2
  //   BANK3
endmodule

module S_MIPS (
  input  Kbd_Available,
  input  [6:0] Kbd_ASCII_Data,
  input  [31:0] RAM_Out_0,
  input  [31:0] RAM_Out_1,
  input  Reset,
  input  [31:0] RAM_Out_2,
  input  Clock,
  input  [31:0] RAM_Out_3,
  input  [3:0] Read_Time,
  input  [3:0] Write_Time,
  output Kbd_Enable,
  output [15:0] Address,
  output Kbd_Clear,
  output TTY_Enable,
  output [6:0] TTY_ASCII_Data,
  output Stop,
  output [31:0] RAM_In_0,
  output [31:0] RAM_In_1,
  output [31:0] RAM_In_2,
  output [31:0] RAM_In_3,
  output [3:0] Mask,
  output nRead_Write,
  output Chip_Select
);


  // Other names for the same wires on the sheet: CLK = Clock; CLR = Reset; CS = Chip_Select;
  //   KBD_AVAIL = Kbd_Available; KBD_CLR = Kbd_Clear; KBD_DATA[6:0] = Kbd_ASCII_Data; RAM_A[15:0] = Address;
  //   RAM_INPUT_0[31:0] = RAM_In_0; RAM_INPUT_1[31:0] = RAM_In_1; RAM_INPUT_2[31:0] = RAM_In_2;
  //   RAM_INPUT_3[31:0] = RAM_In_3; RAM_MASK[3:0] = Mask; RAM_OUTPUT_0[31:0] = RAM_Out_0;
  //   RAM_OUTPUT_1[31:0] = RAM_Out_1; RAM_OUTPUT_2[31:0] = RAM_Out_2; RAM_OUTPUT_3[31:0] = RAM_Out_3;
  //   RW = nRead_Write; TTY_DATA[6:0] = TTY_ASCII_Data

  // Notes on the sheet:
  //   RAM ADDRESS
  //   DATA FROM RAM
  //   DATA TO RAM
  //   DATA WRITE MASK
  //   RAM TIMING
  //   RAM CONTROL
  //   KEYBOARD
  //   TTY
  //   SEQUENCING
endmodule

module RAM_Dispatcher (
  input  [3:0] WriteTime,
  input  Clock,
  input  CLR,
  output [31:0] Data,
  output [15:0] Address,
  output [3:0] Mask,
  output Finished,
  output Write
);

  wire demultiplexer_2_out1, demultiplexer_3_out1, End, IDLE_q, IncAddr, Load, or_1_out, or_2_out, While_q,
       WriteEnd;
  wire [3:0] counter_1_q;
  wire [31:0] CurrentAddress_q;

  Counter #(.width(32), .max('hffffffff)) CurrentAddress (
    .count(IncAddr), .Q({CurrentAddress_q[31:18], Address, CurrentAddress_q[1:0]}), .clk(Clock), .clr(CLR));  // open: load, D, carry
  or or_1 (or_1_out, IncAddr, demultiplexer_3_out1, Finished);
  D_Flip_Flop IDLE (.clk(Clock), .D(or_1_out), .Q(IDLE_q), .preset(CLR));  // open: Qn, en, reset
  Demultiplexer #(.enable("false")) demultiplexer_1 (.out0(Load), .out1(Finished), .in(IDLE_q), .sel(End));
  D_Flip_Flop While (.clk(Clock), .D(or_2_out), .Q(While_q), .reset(CLR));  // open: Qn, preset, en
  or or_2 (or_2_out, Write, Load);
  RAM_part #(.addrWidth(18), .dataWidth(32)) ram_1 (
    .addr({Address, CurrentAddress_q[1:0]}), .data(Data), .clk(Clock));  // open: sel, ld, clr
  Demultiplexer #(.enable("false")) demultiplexer_2 (
    .out0(Write), .out1(demultiplexer_2_out1), .in(While_q), .sel(WriteEnd));
  Decoder #(.select(2)) decoder_1 (
    .out0(Mask[0]), .out1(Mask[1]), .out2(Mask[2]), .out3(Mask[3]), .sel(CurrentAddress_q[1:0]));  // open: en
  Demultiplexer #(.enable("false")) demultiplexer_3 (
    .out0(IncAddr), .out1(demultiplexer_3_out1), .in(demultiplexer_2_out1), .sel(End));
  Counter #(.width(4), .max('hf)) counter_1 (
    .load(Load), .D(WriteTime), .count(Write), .Q(counter_1_q), .clk(Clock));  // open: carry, clr
  Comparator #(.width(32)) comparator_1 (.a(Data), .b({32{1'b1}}), .eq(End));  // open: gt, lt
  Comparator #(.width(4)) comparator_2 (.a(4'b0000), .b(counter_1_q), .eq(WriteEnd));  // open: gt, lt

  // Other names for the same wires on the sheet: CLK = Clock; Count = Write; WT[3:0] = WriteTime
endmodule

module ALU (
  input  [31:0] A,
  input  [31:0] B,
  input  [3:0] Operation,
  input  M_D,
  input  [31:0] SP,
  input  in_6,
  output [31:0] R,
  output [31:0] H,
  output [31:0] L
);

  wire comparator_1_lt, comparator_2_lt;
  wire [3:0] divider_2_out;
  wire [31:0] And, Div, High, Mod, mod_t, Mult, Nor, Or, SC, SD, Slt, Sltu, SM, Subs, Sum, UC, UD, UM, Xor;

  // Probe on A
  // Probe on B
  Adder #(.width(32)) adder_1 (.a(A), .b(B), .out(Sum));  // open: cin, cout
  Subtractor #(.width(32)) subtractor_1 (.a(A), .b(B), .out(Subs));  // open: bin, bout
  Multiplier #(.width(32)) multiplier_1 (.a(A), .b(B), .out(Mult));  // open: cin, cout
  Divider #(.width(32)) divider_1 (.a(A), .b(B), .out(Div), .rem(Mod));  // open: upper
  assign And = A & B;  // AND_Gate and_1, 32 bits wide
  assign Or = A | B;  // OR_Gate or_1, 32 bits wide
  assign Xor = A ^ B;  // XOR_Gate xor_1, 32 bits wide
  assign Nor = ~(A | B);  // NOR_Gate nor_1, 32 bits wide
  Comparator #(.width(32)) comparator_1 (.a(A), .b(B), .lt(comparator_1_lt));  // open: gt, eq
  Comparator #(.width(32)) comparator_2 (.a(A), .b(B), .lt(comparator_2_lt));  // open: gt, eq
  assign Slt = {{31{1'b0}}, comparator_1_lt};  // Bit_Extender bit_extender_1
  assign Sltu = {{31{1'b0}}, comparator_2_lt};  // Bit_Extender bit_extender_2
  Divition divition_1 (.A(A), .B(B), .Signed_div(SD), .unsigned_div(UD), .mod(mod_t));
  Multiplication multiplication_1 (
    .A(A), .B(B), .unsigned_mult(UM), .signed_mult(SM), .unsigned_current(UC), .signed_current(SC));
  Divider #(.width(4)) divider_2 (.a(Operation), .b(4'b0010), .out(divider_2_out));  // open: upper, rem
  Multiplexer #(.select(2), .width(32), .enable("false")) multiplexer_1 (
    .in0(UC), .in1(SC), .in2(Mod), .in3(mod_t), .out(High), .sel(divider_2_out[1:0]));
  Multiplexer #(.select(4), .width(32)) multiplexer_2 (
    .in0(Sum), .in1(Subs), .in2(SM), .in3(UM), .in4(SD), .in5(UD), .in6(And), .in7(Or), .in8(Nor), .in9(Xor),
    .in10(Slt), .in11(Sltu), .in15({32{1'b0}}), .out(R), .sel(Operation));  // open: in12, in13, in14, en
  Register #(.width(32)) u_high (.D(High), .en(M_D), .Q(H), .clk(in_6));  // open: clr
  Register #(.width(32)) low (.D(R), .en(M_D), .Q(L), .clk(in_6));  // open: clr

  // Other names for the same wires on the sheet: Clock = in_6; Low[31:0] = R; Mult_Div = M_D; Op[3:0] = Operation

  // Notes on the sheet:
  //   Inputs
  //   Outputs
endmodule

module Divition (
  input  [31:0] A,
  input  [31:0] B,
  output [31:0] Signed_div,
  output [31:0] unsigned_div,
  output [31:0] mod
);

  wire [31:0] a_compl, b_compl, multiplexer_1_out, multiplexer_2_out, not_1_out, not_2_out;

  assign not_1_out = ~A;  // NOT_Gate not_1, 32 bits wide
  Adder #(.width(32)) adder_1 (.a(not_1_out), .b(32'h1), .out(a_compl));  // open: cin, cout
  assign not_2_out = ~B;  // NOT_Gate not_2, 32 bits wide
  Adder #(.width(32)) adder_2 (.a(not_2_out), .b(32'h1), .out(b_compl));  // open: cin, cout
  Multiplexer #(.width(32)) multiplexer_1 (.in0(A), .in1(a_compl), .out(multiplexer_1_out), .sel(A[31]));  // open: en
  Multiplexer #(.width(32)) multiplexer_2 (.in0(B), .in1(b_compl), .out(multiplexer_2_out), .sel(B[31]));  // open: en
  Divider #(.width(32)) divider_1 (.a(A), .b(B), .out(Signed_div), .upper({32{1'b0}}));  // open: rem
  Divider #(.width(32)) divider_2 (
    .a(multiplexer_1_out), .b(multiplexer_2_out), .out(unsigned_div), .upper({32{1'b0}}), .rem(mod));

  // Other names for the same wires on the sheet: a_sign = A[31]; b_sign = B[31]; module[31:0] = mod

  // Notes on the sheet:
  //   OUTPUTS
endmodule

module Multiplication (
  input  [31:0] A,
  input  [31:0] B,
  output [31:0] unsigned_mult,
  output [31:0] signed_mult,
  output [31:0] unsigned_current,
  output [31:0] signed_current
);

  wire [31:0] a_compl, b_compl, multiplexer_1_out, multiplexer_2_out, not_1_out, not_2_out;

  assign not_1_out = ~A;  // NOT_Gate not_1, 32 bits wide
  Adder #(.width(32)) adder_1 (.a(not_1_out), .b(32'h1), .out(a_compl));  // open: cin, cout
  assign not_2_out = ~B;  // NOT_Gate not_2, 32 bits wide
  Adder #(.width(32)) adder_2 (.a(not_2_out), .b(32'h1), .out(b_compl));  // open: cin, cout
  Multiplexer #(.width(32)) multiplexer_1 (.in0(A), .in1(a_compl), .out(multiplexer_1_out), .sel(A[31]));  // open: en
  Multiplexer #(.width(32)) multiplexer_2 (.in0(B), .in1(b_compl), .out(multiplexer_2_out), .sel(B[31]));  // open: en
  Multiplier #(.width(32)) multiplier_1 (.a(A), .b(B), .out(signed_mult), .cin({32{1'b0}}), .cout(signed_current));
  Multiplier #(.width(32)) multiplier_2 (
    .a(multiplexer_1_out), .b(multiplexer_2_out), .out(unsigned_mult), .cin({32{1'b0}}),
    .cout(unsigned_current));

  // Other names for the same wires on the sheet: a_sign = A[31]; b_sign = B[31]

  // Notes on the sheet:
  //   OUTPUTS
endmodule

module Instruction_decoder (
  input  [31:0] instruction,
  output [4:0] Data_Address,
  output [4:0] Sa,
  output [4:0] Sb,
  output [25:0] Destino_Salto,
  output Mult_Div,
  output R_W,
  output [3:0] Op_ALU,
  output [31:0] K,
  output Tipo_I,
  output R,
  output [2:0] Selector_Branch,
  output jump,
  output ALU_instr,
  output pop,
  output push,
  output halt,
  output tty,
  output rnd,
  output kbd,
  output mfhi,
  output mflo,
  output lw,
  output sw,
  output mem_inst,
  output stack,
  output write_inst,
  output _1_cycle_instruction
);

  wire add, addi, \and , andi, beq, bgtz, blez, bltz, bne, comparator_18_eq, comparator_19_eq,
       comparator_20_eq, comparator_21_eq, comparator_22_eq, comparator_23_eq, comparator_24_eq,
       comparator_25_eq, comparator_26_eq, comparator_27_eq, comparator_28_eq, comparator_29_eq,
       comparator_30_eq, comparator_31_eq, comparator_32_eq, comparator_33_eq, comparator_34_eq,
       comparator_35_eq, comparator_36_eq, comparator_37_eq, comparator_38_eq, comparator_39_eq, div, divu,
       j, jr, mult, mulu, nop, \nor , oper, \or , or_2_out, or_3_out, or_4_out, or_5_out, or_6_out, ori, slt,
       slti, sltiu, sltu, special, sub, Tipo_R, \xor , xori;

  or or_1 (divu, \and , andi);
  Comparator #(.width(6)) comparator_1 (.a(instruction[31:26]), .b({6{1'b0}}), .eq(oper));  // open: gt, lt
  Comparator #(.width(6)) comparator_2 (.a(instruction[31:26]), .b(6'b111000), .eq(stack));  // open: gt, lt
  Comparator #(.width(6)) comparator_3 (.a(instruction[31:26]), .b({6{1'b1}}), .eq(special));  // open: gt, lt
  Comparator #(.width(6)) comparator_4 (.a(instruction[31:26]), .b(6'b001000), .eq(addi));  // open: gt, lt
  Comparator #(.width(6)) comparator_5 (.a(instruction[31:26]), .b(6'b001100), .eq(andi));  // open: gt, lt
  Comparator #(.width(6)) comparator_6 (.a(instruction[31:26]), .b(6'b001101), .eq(ori));  // open: gt, lt
  Comparator #(.width(6)) comparator_7 (.a(instruction[31:26]), .b(6'b001110), .eq(xori));  // open: gt, lt
  Comparator #(.width(6)) comparator_8 (.a(instruction[31:26]), .b(6'b001010), .eq(slti));  // open: gt, lt
  Comparator #(.width(6)) comparator_9 (.a(instruction[31:26]), .b(6'b001011), .eq(sltiu));  // open: gt, lt
  Comparator #(.width(6)) comparator_10 (.a(instruction[31:26]), .b(6'b000100), .eq(beq));  // open: gt, lt
  Comparator #(.width(6)) comparator_11 (.a(instruction[31:26]), .b(6'b000101), .eq(bne));  // open: gt, lt
  Comparator #(.width(6)) comparator_12 (.a(instruction[31:26]), .b(6'b000110), .eq(blez));  // open: gt, lt
  Comparator #(.width(6)) comparator_13 (.a(instruction[31:26]), .b(6'b000111), .eq(bgtz));  // open: gt, lt
  Comparator #(.width(6)) comparator_14 (.a(instruction[31:26]), .b(6'b000001), .eq(bltz));  // open: gt, lt
  Comparator #(.width(6)) comparator_15 (.a(instruction[31:26]), .b(6'b100011), .eq(lw));  // open: gt, lt
  Comparator #(.width(6)) comparator_16 (.a(instruction[31:26]), .b(6'b101011), .eq(sw));  // open: gt, lt
  Comparator #(.width(6)) comparator_17 (.a(instruction[31:26]), .b(6'b000010), .eq(j));  // open: gt, lt
  or or_2 (or_2_out, add, addi, lw, sw);
  or or_3 (or_3_out, \or , ori);
  or or_4 (or_4_out, \xor , xori);
  or or_5 (or_5_out, slt, slti);
  or or_6 (or_6_out, sltu, sltiu);
  // Probe on instruction[25:21]
  or or_7 (Tipo_R, oper, stack, special);
  or or_8 (ALU_instr, \or , andi, add, addi, sub, mult, mulu, div, divu, \and , ori, xori, slti, sltiu, mfhi, mflo, \nor , \xor , slt, sltu);
  or or_9 (Tipo_I, addi, andi, ori, xori, slti, sltiu, beq, bne, blez, bgtz, bltz, lw, sw);
  Operation_ALU Operation_ALU (
    .Addition(or_2_out), .Substract(sub), .Multiply(mult), .Mult_unsigned(mulu), .Divition(div),
    .Div_unsigned(divu), .Logical_and(divu), .Logical_or(or_3_out), .Logical_nor(\nor ),
    .Logical_xor(or_4_out), .Move_from_Hi(mfhi), .Move_from_lo(mflo), .Set_less_than(or_5_out),
    .Unsigned_set_less_than(or_6_out), .Selector_ALU(Op_ALU));
  and and_1 (add, Tipo_R, comparator_18_eq);
  Comparator #(.width(6)) comparator_18 (.a(instruction[5:0]), .b(6'b100000), .eq(comparator_18_eq));  // open: gt, lt
  and and_2 (sub, Tipo_R, comparator_19_eq);
  Comparator #(.width(6)) comparator_19 (.a(instruction[5:0]), .b(6'b100010), .eq(comparator_19_eq));  // open: gt, lt
  and and_3 (mult, Tipo_R, comparator_20_eq);
  Comparator #(.width(6)) comparator_20 (.a(instruction[5:0]), .b(6'b011000), .eq(comparator_20_eq));  // open: gt, lt
  and and_4 (mulu, Tipo_R, comparator_21_eq);
  Comparator #(.width(6)) comparator_21 (.a(instruction[5:0]), .b(6'b011001), .eq(comparator_21_eq));  // open: gt, lt
  and and_5 (div, Tipo_R, comparator_22_eq);
  Comparator #(.width(6)) comparator_22 (.a(instruction[5:0]), .b(6'b011010), .eq(comparator_22_eq));  // open: gt, lt
  and and_6 (divu, Tipo_R, comparator_23_eq);
  Comparator #(.width(6)) comparator_23 (.a(instruction[5:0]), .b(6'b011011), .eq(comparator_23_eq));  // open: gt, lt
  and and_7 (\and , Tipo_R, comparator_24_eq);
  Comparator #(.width(6)) comparator_24 (.a(instruction[5:0]), .b(6'b100100), .eq(comparator_24_eq));  // open: gt, lt
  and and_8 (\or , Tipo_R, comparator_25_eq);
  Comparator #(.width(6)) comparator_25 (.a(instruction[5:0]), .b(6'b100101), .eq(comparator_25_eq));  // open: gt, lt
  and and_9 (\nor , Tipo_R, comparator_26_eq);
  Comparator #(.width(6)) comparator_26 (.a(instruction[5:0]), .b(6'b100111), .eq(comparator_26_eq));  // open: gt, lt
  and and_10 (\xor , Tipo_R, comparator_27_eq);
  Comparator #(.width(6)) comparator_27 (.a(instruction[5:0]), .b(6'b101000), .eq(comparator_27_eq));  // open: gt, lt
  and and_11 (slt, Tipo_R, comparator_28_eq);
  Comparator #(.width(6)) comparator_28 (.a(instruction[5:0]), .b(6'b101010), .eq(comparator_28_eq));  // open: gt, lt
  and and_12 (sltu, Tipo_R, comparator_29_eq);
  Comparator #(.width(6)) comparator_29 (.a(instruction[5:0]), .b(6'b101011), .eq(comparator_29_eq));  // open: gt, lt
  and and_13 (mfhi, Tipo_R, comparator_30_eq);
  Comparator #(.width(6)) comparator_30 (.a(instruction[5:0]), .b(6'b010000), .eq(comparator_30_eq));  // open: gt, lt
  and and_14 (mflo, Tipo_R, comparator_31_eq);
  Comparator #(.width(6)) comparator_31 (.a(instruction[5:0]), .b(6'b010010), .eq(comparator_31_eq));  // open: gt, lt
  Comparator #(.width(6)) comparator_32 (.a(instruction[5:0]), .b({6{1'b0}}), .eq(comparator_32_eq));  // open: gt, lt
  and and_15 (jr, Tipo_R, comparator_33_eq);
  Comparator #(.width(6)) comparator_33 (.a(instruction[5:0]), .b(6'b001000), .eq(comparator_33_eq));  // open: gt, lt
  Comparator #(.width(6)) comparator_34 (.a(instruction[5:0]), .b({6{1'b0}}), .eq(comparator_34_eq));  // open: gt, lt
  Comparator #(.width(6)) comparator_35 (.a(instruction[5:0]), .b(6'b000001), .eq(comparator_35_eq));  // open: gt, lt
  Comparator #(.width(6)) comparator_36 (.a(instruction[5:0]), .b({6{1'b1}}), .eq(comparator_36_eq));  // open: gt, lt
  Comparator #(.width(6)) comparator_37 (.a(instruction[5:0]), .b(6'b000001), .eq(comparator_37_eq));  // open: gt, lt
  Comparator #(.width(6)) comparator_38 (.a(instruction[5:0]), .b(6'b000010), .eq(comparator_38_eq));  // open: gt, lt
  Comparator #(.width(6)) comparator_39 (.a(instruction[5:0]), .b(6'b000100), .eq(comparator_39_eq));  // open: gt, lt
  or or_10 (mem_inst, sw, lw);
  or or_11 (write_inst, sw, push);
  or or_12 (R, rnd, mflo, kbd, mfhi, tty);
  and and_16 (nop, oper, comparator_32_eq);
  and and_17 (pop, stack, comparator_34_eq);
  and and_18 (push, stack, comparator_35_eq);
  and and_19 (halt, special, comparator_36_eq);
  and and_20 (tty, special, comparator_37_eq);
  and and_21 (rnd, special, comparator_38_eq);
  and and_22 (kbd, special, comparator_39_eq);
  nor nor_1 (_1_cycle_instruction, lw, stack, sw);
  Multiplexer #(.width(5)) multiplexer_1 (
    .in0(instruction[15:11]), .in1(instruction[20:16]), .out(Data_Address), .sel(Tipo_I), .en(1'b1));
  Multiplexer #(.width(5), .enable("false")) multiplexer_2 (
    .in0(instruction[25:21]), .in1(instruction[20:16]), .out(Sa), .sel(1'b0));
  Multiplexer #(.width(5), .enable("false")) multiplexer_3 (
    .in0(instruction[20:16]), .in1(instruction[25:21]), .out(Sb), .sel(1'b0));
  or or_13 (Mult_Div, mult, mulu, div, divu);
  Branch_Jump Branch_Jump (
    .Branch_on_equal(beq), .Branch_on_not_equal(bne), .Branch_on_less_than_or_equal_zero(blez),
    .Branch_on_greater_than_zero(bgtz), .Branch_on_less_than_zero(bltz), .Jump(j), .Jump_register(jr),
    .Branch_Selector(Selector_Branch));
  or or_14 (jump, beq, bne, blez, bgtz, bltz, j, jr, nop);
  or or_15 (R_W, divu, divu, divu, divu, divu, divu, divu, divu, divu, divu, divu, divu, divu, divu, divu, divu, divu, divu, divu);
  assign K = {{16{instruction[15]}}, instruction[15:0]};  // Bit_Extender bit_extender_1

  assign Destino_Salto = instruction[25:0];

  // Other names for the same wires on the sheet: Constante[15:0] = instruction[15:0];
  //   Function_Code[5:0] = instruction[5:0]; Rd[4:0] = instruction[15:11]; Rt[4:0] = instruction[20:16];
  //   Rs[4:0] = instruction[25:21]; Op_Code[5:0] = instruction[31:26]; Tipo_J = j

  // Notes on the sheet:
  //   FORMATO R
  //   FORMATO I
  //   FORMATO J
  //   Outputs
endmodule

module Operation_ALU (
  input  Addition,
  input  Substract,
  input  Multiply,
  input  Mult_unsigned,
  input  Divition,
  input  Div_unsigned,
  input  Logical_and,
  input  Logical_or,
  input  Logical_nor,
  input  Logical_xor,
  input  Move_from_Hi,
  input  Move_from_lo,
  input  Set_less_than,
  input  Unsigned_set_less_than,
  output [3:0] Selector_ALU
);

  wire not_1_out, not_2_out, not_3_out, not_4_out, not_5_out, not_6_out, not_7_out, not_8_out, not_9_out,
       not_10_out, not_11_out, not_12_out, not_13_out, not_14_out, not_15_out, not_16_out, not_17_out,
       not_18_out, not_19_out, not_20_out, not_21_out, not_22_out, not_23_out, not_24_out, not_25_out,
       not_26_out, not_27_out, not_28_out, not_29_out, not_30_out, not_31_out;

  not not_1 (not_1_out, Addition);
  not not_2 (not_2_out, Multiply);
  not not_3 (not_3_out, Div_unsigned);
  not not_4 (not_4_out, Logical_and);
  not not_5 (not_5_out, Logical_nor);
  not not_6 (not_6_out, Set_less_than);
  not not_7 (not_7_out, Move_from_Hi);
  not not_8 (not_8_out, Addition);
  not not_9 (not_9_out, Substract);
  not not_10 (not_10_out, Div_unsigned);
  not not_11 (not_11_out, Divition);
  not not_12 (not_12_out, Logical_nor);
  not not_13 (not_13_out, Logical_xor);
  not not_14 (not_14_out, Move_from_Hi);
  not not_15 (not_15_out, Move_from_lo);
  and and_1 (Selector_ALU[0], not_1_out, not_2_out, not_3_out, not_4_out, not_5_out, not_6_out, not_7_out);
  and and_2 (Selector_ALU[1], not_8_out, not_9_out, not_10_out, not_11_out, not_12_out, not_13_out, not_14_out, not_15_out);
  not not_16 (not_16_out, Addition);
  not not_17 (not_17_out, Substract);
  not not_18 (not_18_out, Addition);
  not not_19 (not_19_out, Substract);
  not not_20 (not_20_out, Multiply);
  not not_21 (not_21_out, Mult_unsigned);
  not not_22 (not_22_out, Div_unsigned);
  not not_23 (not_23_out, Divition);
  not not_24 (not_24_out, Logical_and);
  not not_25 (not_25_out, Logical_or);
  not not_26 (not_26_out, Multiply);
  not not_27 (not_27_out, Mult_unsigned);
  not not_28 (not_28_out, Logical_nor);
  not not_29 (not_29_out, Logical_xor);
  not not_30 (not_30_out, Set_less_than);
  not not_31 (not_31_out, Unsigned_set_less_than);
  and and_3 (Selector_ALU[2], not_16_out, not_17_out, not_26_out, not_27_out, not_28_out, not_29_out, not_30_out, not_31_out);
  and and_4 (Selector_ALU[3], not_18_out, not_19_out, not_20_out, not_21_out, not_22_out, not_23_out, not_24_out, not_25_out);

  // Other names for the same wires on the sheet: add = Addition; and = Logical_and; div = Divition;
  //   divu = Div_unsigned; mfhi = Move_from_Hi; mflo = Move_from_lo; mult = Multiply; mulu = Mult_unsigned;
  //   nor = Logical_nor; or = Logical_or; Bit_1 = Selector_ALU[0]; Bit_2 = Selector_ALU[1]; Bit_3 = Selector_ALU[2];
  //   Bit_4 = Selector_ALU[3]; slt = Set_less_than; sltu = Unsigned_set_less_than; sub = Substract; xor = Logical_xor
endmodule

module Branch_Jump (
  input  Branch_on_equal,
  input  Branch_on_not_equal,
  input  Branch_on_less_than_or_equal_zero,
  input  Branch_on_greater_than_zero,
  input  Branch_on_less_than_zero,
  input  Jump,
  input  Jump_register,
  output [2:0] Branch_Selector
);

  wire not_1_out, not_2_out, not_3_out, not_4_out, not_5_out, not_6_out, not_7_out, not_8_out, not_9_out,
       not_10_out, not_11_out, not_12_out;

  not not_1 (not_1_out, Branch_on_equal);
  not not_2 (not_2_out, Branch_on_less_than_or_equal_zero);
  not not_3 (not_3_out, Branch_on_less_than_zero);
  not not_4 (not_4_out, Jump_register);
  not not_5 (not_5_out, Branch_on_equal);
  not not_6 (not_6_out, Branch_on_not_equal);
  not not_7 (not_7_out, Branch_on_less_than_zero);
  not not_8 (not_8_out, Jump);
  not not_9 (not_9_out, Branch_on_equal);
  not not_10 (not_10_out, Branch_on_not_equal);
  not not_11 (not_11_out, Branch_on_less_than_or_equal_zero);
  not not_12 (not_12_out, Branch_on_greater_than_zero);
  and and_1 (Branch_Selector[0], not_1_out, not_2_out, not_3_out, not_4_out);
  and and_2 (Branch_Selector[1], not_5_out, not_6_out, not_7_out, not_8_out);
  and and_3 (Branch_Selector[2], not_9_out, not_10_out, not_11_out, not_12_out);

  // Other names for the same wires on the sheet: beq = Branch_on_equal; bgtz = Branch_on_greater_than_zero;
  //   blez = Branch_on_less_than_or_equal_zero; bltz = Branch_on_less_than_zero; bne = Branch_on_not_equal;
  //   bit_1 = Branch_Selector[0]; bit_2 = Branch_Selector[1]; bit_3 = Branch_Selector[2]; j = Jump;
  //   jr = Jump_register
endmodule

module Data_Path (
  input  Kbd_Available,
  input  Reset,
  input  [31:0] RAM_Out_0,
  input  Clock,
  input  [6:0] Kbd_ASCII_Data,
  input  [31:0] RAM_Out_1,
  input  [31:0] RAM_Out_2,
  input  [31:0] RAM_Out_3,
  input  [3:0] Read_Time,
  input  [3:0] Write_Time,
  output [31:0] Memorie_Address,
  output [31:0] R,
  output jmp,
  output ALU_inst,
  output Memorie_Inst,
  output Stack_inst,
  output Write_inst,
  output R_instr,
  output stop,
  output tty_en,
  output [6:0] tty_data
);

  wire _1cycle, Cache_working, CS1, EGI, Enable_PC, Inmediate, instruction_decoder_1_p2,
       instruction_decoder_1_p5, Is_PC, KBD_ENABLE, lw, mfhi, mflo, Mult_Div, pop, push, Read_Write, RF_RW,
       Rnd, sw;
  wire [2:0] Sb;
  wire [3:0] Operation;
  wire [4:0] Data_Address, Selector_A, Selector_B;
  wire [25:0] Destino_Salto;
  wire [31:0] B, Constant, HI, IA_prime, Inst_Reg_output, Instruction, LO, multiplexer_1_out, PC, Result, SP;
  wire [31:7] A;

  Branch_Control branch_control_1 (
    .in_1(jmp), .in_2({A, tty_data}), .in_3(B), .in_4(PC), .in_5(Destino_Salto), .in_6(Sb), .in_7(Constant),
    .IA_prime(IA_prime));
  Register_File register_file_1 (
    .DA(Data_Address), .ALU(Result), .R_W(RF_RW), .Inst(Instruction), .SA(Selector_A), .HI(HI), .Clk(Clock),
    .LO(LO), .Mem_RW(Enable_PC), .Reset(Reset), .Random(Rnd), .Pop(pop), .Push(push), .lw(lw), .mfhi(mfhi),
    .mflo(mflo), .rnd(Rnd), .kbd(KBD_ENABLE), .Kbd_ASCII_Data(Kbd_ASCII_Data), .A({A, tty_data}), .B(B),
    .SP(SP));  // open: SB
  Instruction_Memory__Cache instruction_memory_cache_1 (
    .Ready(EGI), .Reset(Reset), .Get(Enable_PC), .Halt(stop), .Cache_on_work(Cache_working),
    .Data_output(Instruction), .Clock(Clock), .Chip_Select(CS1));  // open: Address, Read_Time, RO0, RO2, RO1, RO3, Write_RAM, RAM_Address
  Program_Counter program_counter_1 (.IA_prime(IA_prime), .Clock(Clock), .Enable(Enable_PC), .Reset(Reset), .PC(PC));
  Multiplexer #(.width(32)) multiplexer_1 (
    .in0(B), .in1(Constant), .out(multiplexer_1_out), .sel(Inmediate));  // open: en
  ALU alu_1 (
    .A({A, tty_data}), .B(multiplexer_1_out), .Operation(Operation), .M_D(Mult_Div), .in_6(Clock), .L(LO),
    .H(HI), .R(Result), .SP(SP));
  Memorie_Address memorie_address_1 (
    .PC(PC), .ALU(Result), .SP(SP), .lw(lw), .sw(sw), .pop(pop), .push(push), .pc_2(Is_PC),
    .Memorie_Address(Memorie_Address));
  Instruction_Register Inst_Reg (
    .Instruction(Instruction), .Clock(Clock), .Reset(Reset), .Enable(EGI), .Output(Inst_Reg_output));  // open: Instruction_Charged
  // Instruction_decoder instruction_decoder_1: pin names not known; wires that end beside it: Inst_Reg_output, instruction_decoder_1_p2, instruction_decoder_1_p2, pop, instruction_decoder_1_p5, instruction_decoder_1_p5, push, stop, tty_en, Rnd, KBD_ENABLE, mfhi, mflo, lw, sw, Data_Address, Selector_A, Selector_B, Read_Write, Mult_Div, Constant, Inmediate, Destino_Salto, jmp, ALU_inst, R_instr, Sb, Operation, Memorie_Inst, Stack_inst, Write_inst, _1cycle
  control_unit_cache control_unit_cache_1 (
    .Cache_Working(Cache_working), .Enable(Enable_PC), .Clock(Clock), .IMR(EGI), .II(_1cycle));  // open: Write_Register, DMR, Chip_Select
  Memorie memorie_1 (
    .Address(Result), .RAM_Out_0(RAM_Out_0), .RAM_Out_1(RAM_Out_1), .RAM_Out_2(RAM_Out_2),
    .RAM_Out_3(RAM_Out_3));  // open: Data_0, Data_In_1, Data_In_2, Data_In_3, address_2, mask, CS, in_6, RW, in_7, ready_inst, Clock, ready_data, Reset, ready_write, Write, Obtain_Inst, Obtain_Data, Is_Instruction, Halt, Finished, Write_RAM, MAddress, Instruction
  Multiplexer #(.width(32), .enable("false")) multiplexer_2 (.in0({A, tty_data}), .in1(B), .out(R), .sel(sw));

  // Other names for the same wires on the sheet: A[6:0] = tty_data; ALU_instruction = ALU_inst; CLK = Clock;
  //   CLR = Reset; KBD_AVAIL = Kbd_Available; KBD_DATA[6:0] = Kbd_ASCII_Data; Memorie_Instruction = Memorie_Inst;
  //   RAM_OUTPUT_0[31:0] = RAM_Out_0; RAM_OUTPUT_1[31:0] = RAM_Out_1; RAM_OUTPUT_2[31:0] = RAM_Out_2;
  //   RAM_OUTPUT_3[31:0] = RAM_Out_3; Stack_Instruction = Stack_inst; Tipo_R = R_instr; TTY_ENABLE = tty_en;
  //   Write_Instruction = Write_inst

  // Notes on the sheet:
  //   DATA FROM RAM
  //   Branch Control
  //   Register File
  //   Program Counter
  //   ALU
  //   Memorie Address
  //   Instruction Decoder
  //   Outputs
endmodule

module Register_File (
  input  [4:0] DA,
  input  [31:0] ALU,
  input  R_W,
  input  [31:0] Inst,
  input  [4:0] SA,
  input  [31:0] HI,
  input  [4:0] SB,
  input  Clk,
  input  [31:0] LO,
  input  Mem_RW,
  input  Reset,
  input  Random,
  input  Pop,
  input  Push,
  input  lw,
  input  mfhi,
  input  mflo,
  input  rnd,
  input  kbd,
  input  [6:0] Kbd_ASCII_Data,
  output [31:0] A,
  output [31:0] B,
  output [31:0] SP
);

  wire L31, or_4_out, or_5_out, R0, R1, R2, R3, R4, R5, R6, R7, R8, R9, R10, R11, R12, R13, R14, R15, R16,
       R17, R18, R19, R20, R21, R22, R23, R24, R25, R26, R27, R28, R29, R30, R31;
  wire [2:0] selector;
  wire [31:0] adder_1_out, D0, D1, D2, D3, D4, D5, D6, D7, D8, D9, D10, D11, D12, D13, D14, D15, D16, D17,
       D18, D19, D20, D21, D22, D23, D24, D25, D26, D27, D28, D29, D30, Di, KBD_DATA, multiplexer_3_out,
       multiplexer_4_out, RND_t, SP_t, subtractor_1_out;

  // Probe on SA
  // Probe on SB
  Random #(.width(32)) random_1 (.clk(Clk), .next(1'b1), .out(RND_t));  // open: clr
  Demultiplexer #(.select(5)) demultiplexer_1 (
    .out0(R0), .out1(R1), .out2(R2), .out3(R3), .out4(R4), .out5(R5), .out6(R6), .out7(R7), .out8(R8),
    .out9(R9), .out10(R10), .out11(R11), .out12(R12), .out13(R13), .out14(R14), .out15(R15), .out16(R16),
    .out17(R17), .out18(R18), .out19(R19), .out20(R20), .out21(R21), .out22(R22), .out23(R23), .out24(R24),
    .out25(R25), .out26(R26), .out27(R27), .out28(R28), .out29(R29), .out30(R30), .out31(R31), .in(R_W),
    .sel(DA));  // open: en
  // Probe on DA
  assign KBD_DATA = {{25{1'b0}}, Kbd_ASCII_Data};  // Bit_Extender bit_extender_1
  or or_1 (selector[0], lw, Pop, mflo, kbd);
  or or_2 (selector[1], mfhi, mflo);
  or or_3 (selector[2], rnd, kbd);
  Register #(.width(32)) u_R0 (.D({32{1'b0}}), .en(R0), .Q(D0), .clk(Clk), .clr(Reset));
  Register #(.width(32)) u_R4 (.D(Di), .en(R4), .Q(D4), .clk(Clk), .clr(Reset));
  Register #(.width(32)) u_R8 (.D(Di), .en(R8), .Q(D8), .clk(Clk), .clr(Reset));
  Register #(.width(32)) u_R12 (.D(Di), .en(R12), .Q(D12), .clk(Clk), .clr(Reset));
  Register #(.width(32)) u_R16 (.D(Di), .en(R16), .Q(D16), .clk(Clk), .clr(Reset));
  Register #(.width(32)) u_R20 (.D(Di), .en(R20), .Q(D20), .clk(Clk), .clr(Reset));
  Register #(.width(32)) u_R24 (.D(Di), .en(R24), .Q(D24), .clk(Clk), .clr(Reset));
  Register #(.width(32)) u_R28 (.D(Di), .en(R28), .Q(D28), .clk(Clk), .clr(Reset));
  Multiplexer #(.select(5), .width(32)) multiplexer_1 (
    .in0(D0), .in1(D1), .in2(D2), .in3(D3), .in4(D4), .in5(D5), .in6(D6), .in7(D7), .in8(D8), .in9(D9),
    .in10(D10), .in11(D11), .in12(D12), .in13(D13), .in14(D14), .in15(D15), .in16(D16), .in17(D17),
    .in18(D18), .in19(D19), .in20(D20), .in21(D21), .in22(D22), .in23(D23), .in24(D24), .in25(D25),
    .in26(D26), .in27(D27), .in28(D28), .in29(D29), .in30(D30), .in31(SP), .out(A), .sel(SA));  // open: en
  Register #(.width(32)) u_R1 (.D(Di), .en(R1), .Q(D1), .clk(Clk), .clr(Reset));
  Register #(.width(32)) u_R5 (.D(Di), .en(R5), .Q(D5), .clk(Clk), .clr(Reset));
  Register #(.width(32)) u_R9 (.D(Di), .en(R9), .Q(D9), .clk(Clk), .clr(Reset));
  Register #(.width(32)) u_R13 (.D(Di), .en(R13), .Q(D13), .clk(Clk), .clr(Reset));
  Register #(.width(32)) u_R17 (.D(Di), .en(R17), .Q(D17), .clk(Clk), .clr(Reset));
  Register #(.width(32)) u_R21 (.D(Di), .en(R21), .Q(D21), .clk(Clk), .clr(Reset));
  Register #(.width(32)) u_R25 (.D(Di), .en(R25), .Q(D25), .clk(Clk), .clr(Reset));
  Register #(.width(32)) u_R29 (.D(Di), .en(R29), .Q(D29), .clk(Clk), .clr(Reset));
  Multiplexer #(.select(3), .width(32), .enable("false")) multiplexer_2 (
    .in0(ALU), .in1(Inst), .in2(HI), .in3(LO), .in4(RND_t), .in5(KBD_DATA), .out(Di), .sel(selector));  // open: in6, in7
  Register #(.width(32)) u_R2 (.D(Di), .en(R2), .Q(D2), .clk(Clk), .clr(Reset));
  Register #(.width(32)) u_R6 (.D(Di), .en(R6), .Q(D6), .clk(Clk), .clr(Reset));
  Register #(.width(32)) u_R10 (.D(Di), .en(R10), .Q(D10), .clk(Clk), .clr(Reset));
  Register #(.width(32)) u_R14 (.D(Di), .en(R14), .Q(D14), .clk(Clk), .clr(Reset));
  Register #(.width(32)) u_R18 (.D(Di), .en(R18), .Q(D18), .clk(Clk), .clr(Reset));
  Register #(.width(32)) u_R22 (.D(Di), .en(R22), .Q(D22), .clk(Clk), .clr(Reset));
  Register #(.width(32)) u_R26 (.D(Di), .en(R26), .Q(D26), .clk(Clk), .clr(Reset));
  Register #(.width(32)) u_R30 (.D(Di), .en(R30), .Q(D30), .clk(Clk), .clr(Reset));
  Register #(.width(32)) u_R3 (.D(Di), .en(R3), .Q(D3), .clk(Clk), .clr(Reset));
  Register #(.width(32)) u_R7 (.D(Di), .en(R7), .Q(D7), .clk(Clk), .clr(Reset));
  Register #(.width(32)) u_R11 (.D(Di), .en(R11), .Q(D11), .clk(Clk), .clr(Reset));
  Register #(.width(32)) u_R15 (.D(Di), .en(R15), .Q(D15), .clk(Clk), .clr(Reset));
  Register #(.width(32)) u_R19 (.D(Di), .en(R19), .Q(D19), .clk(Clk), .clr(Reset));
  Register #(.width(32)) u_R23 (.D(Di), .en(R23), .Q(D23), .clk(Clk), .clr(Reset));
  Register #(.width(32)) u_R27 (.D(Di), .en(R27), .Q(D27), .clk(Clk), .clr(Reset));
  Subtractor #(.width(32)) subtractor_1 (.a(SP), .b(32'h4), .out(subtractor_1_out));  // open: bin, bout
  Adder #(.width(32)) adder_1 (.a(32'h4), .b(SP), .out(adder_1_out));  // open: cin, cout
  or or_4 (or_4_out, Push, Pop);
  Multiplexer #(.width(32), .enable("false")) multiplexer_3 (.in0(SP_t), .in1(Di), .out(multiplexer_3_out), .sel(R31));
  or or_5 (or_5_out, L31, R31, Reset);
  Multiplexer #(.width(32), .enable("false")) multiplexer_4 (
    .in0(subtractor_1_out), .in1(adder_1_out), .out(multiplexer_4_out), .sel(Pop));
  and and_1 (L31, Mem_RW, or_4_out);
  Multiplexer #(.select(5), .width(32)) multiplexer_5 (
    .in0(D0), .in1(D1), .in2(D2), .in3(D3), .in4(D4), .in5(D5), .in6(D6), .in7(D7), .in8(D8), .in9(D9),
    .in10(D10), .in11(D11), .in12(D12), .in13(D13), .in14(D14), .in15(D15), .in16(D16), .in17(D17),
    .in18(D18), .in19(D19), .in20(D20), .in21(D21), .in22(D22), .in23(D23), .in24(D24), .in25(D25),
    .in26(D26), .in27(D27), .in28(D28), .in29(D29), .in30(D30), .in31(SP), .out(B), .sel(SB));  // open: en
  // Probe on A
  Register #(.width(32)) u_R31 (.D(multiplexer_3_out), .en(or_5_out), .Q(SP), .clk(Clk));  // open: clr
  Multiplexer #(.width(32), .enable("false")) multiplexer_6 (
    .in0(multiplexer_4_out), .in1({32{1'b1}}), .out(SP_t), .sel(Reset));
  // Probe on B

  // Other names for the same wires on the sheet: D31[31:0] = SP; Data_A[31:0] = A; Data_B[31:0] = B;
  //   Instr[31:0] = Inst; is_kbd = kbd; is_rnd = rnd; Rnd_t_t = Random; RS = Reset

  // Notes on the sheet:
  //   Data Address
  //   Read/Write
  //   Selector A
  //   Selector B
  //   Inputs
  //   Registers
  //   Outputs
  //   Data A
  //   Data B
endmodule

module Memorie (
  input  [31:0] Address,
  input  [31:0] RAM_Out_0,
  input  [31:0] RAM_Out_1,
  input  [31:0] RAM_Out_2,
  input  [31:0] RAM_Out_3,
  input  [3:0] in_6,
  input  [3:0] in_7,
  input  Clock,
  input  Reset,
  input  Write,
  input  Obtain_Inst,
  input  Obtain_Data,
  input  Is_Instruction,
  input  Halt,
  input  [31:0] MAddress,
  output [31:0] Data_0,
  output [31:0] Data_In_1,
  output [31:0] Data_In_2,
  output [31:0] Data_In_3,
  output [15:0] address_2,
  output [3:0] mask,
  output CS,
  output [31:0] Instruction,
  output RW,
  output ready_inst,
  output ready_data,
  output Write_RAM,
  output ready_write,
  output Finished
);

  wire CSI, or_1_out, stop;
  wire [31:0] output_instruction_block_0, output_instruction_block_1, output_instruction_block_2,
       output_instruction_block_3;

  or or_1 (or_1_out, Write, stop);
  D_Flip_Flop #(.trigger("falling")) d_ff_1 (.clk(Clock), .D(Write), .Q(RW), .en(or_1_out));  // open: Qn, preset, reset
  Instruction_Memory Instruction_Memory (
    .Address(Address), .output_block_0(output_instruction_block_0), .instruction_block_0(RAM_Out_0),
    .output_block_1(output_instruction_block_1), .instruction_block_1(RAM_Out_1),
    .output_block_2(output_instruction_block_2), .instruction_block_2(RAM_Out_2),
    .output_block_3(output_instruction_block_3), .instruction_block_3(RAM_Out_3), .in_6(in_6), .Clock(Clock),
    .Reset(Reset), .Obtain_Instruction(Obtain_Inst), .Halt(Halt), .Chip_Select(CSI), .Ready(ready_inst));
  Data_Memory Data_Memory (
    .Address(Address), .output_block_0(Data_0), .data_block_0(RAM_Out_0), .output_block_1(Data_In_1),
    .data_block_1(RAM_Out_1), .output_block_2(Data_In_2), .data_block_2(RAM_Out_2),
    .output_block_3(Data_In_3), .data_block_3(RAM_Out_3), .in_6(in_6), .Clock(Clock), .Reset(Reset),
    .Obtain_Data(Obtain_Data), .WCS(Write_RAM), .Ready(ready_data));
  Timer timer_1 (.Time(in_7), .Start(RW), .Ready(stop), .Clock(Clock), .Reset(ready_write));
  Multiplexer #(.select(2), .width(32)) multiplexer_1 (
    .in0(output_instruction_block_0), .in1(output_instruction_block_1), .in2(output_instruction_block_2),
    .in3(output_instruction_block_3), .out(Instruction), .sel(MAddress[3:2]));  // open: en
  D_Flip_Flop #(.trigger("falling")) d_ff_2 (.clk(Clock), .D(stop), .Q(ready_write));  // open: Qn, preset, en, reset
  or or_2 (CS, CSI, Write_RAM, RW);
  Address_Separator address_separator_1 (
    .Address(Address), .Mask(mask), .RAM_Address(address_2));  // open: Output_Selector
  or or_3 (Finished, ready_write, ready_data);

  // Other names for the same wires on the sheet: address_t[15:0] = address_2; Clck = Clock; is_inst = Is_Instruction;
  //   output_data_block_0[31:0] = Data_0; output_data_block_1[31:0] = Data_In_1;
  //   output_data_block_2[31:0] = Data_In_2; output_data_block_3[31:0] = Data_In_3; RAM_OUTPUT_0[31:0] = RAM_Out_0;
  //   RAM_OUTPUT_1[31:0] = RAM_Out_1; RAM_OUTPUT_2[31:0] = RAM_Out_2; RAM_OUTPUT_3[31:0] = RAM_Out_3;
  //   read_time[3:0] = in_6; WCS = Write_RAM; write_time[3:0] = in_7

  // Notes on the sheet:
  //   DATA FROM RAM
  //   DATA TO RAM
endmodule

module Instruction_Memory (
  input  [31:0] Address,
  input  [31:0] instruction_block_0,
  input  [31:0] instruction_block_1,
  input  [31:0] instruction_block_2,
  input  [31:0] instruction_block_3,
  input  [3:0] in_6,
  input  Clock,
  input  Reset,
  input  Obtain_Instruction,
  input  Halt,
  output [31:0] output_block_0,
  output [31:0] output_block_1,
  output [31:0] output_block_2,
  output [31:0] output_block_3,
  output Chip_Select,
  output Ready
);

  wire CS1, CS2, or_1_out, timer_1_ready;

  D_Flip_Flop #(.trigger("falling")) d_ff_1 (
    .clk(Clock), .D(Obtain_Instruction), .Q(CS1), .en(or_1_out));  // open: Qn, preset, reset
  or or_1 (or_1_out, Obtain_Instruction, timer_1_ready);
  Register #(.width(32)) register_1 (.D(instruction_block_0), .en(CS2), .Q(output_block_0), .clk(Clock), .clr(Reset));
  Register #(.width(32)) register_2 (.D(instruction_block_1), .en(CS2), .Q(output_block_1), .clk(Clock), .clr(Reset));
  Register #(.width(32)) register_3 (.D(instruction_block_2), .en(CS2), .Q(output_block_2), .clk(Clock), .clr(Reset));
  Register #(.width(32)) register_4 (.D(instruction_block_3), .en(CS2), .Q(output_block_3), .clk(Clock), .clr(Reset));
  Timer timer_1 (.Time(in_6), .Start(CS1), .Ready(timer_1_ready), .Clock(Clock), .Reset(Ready));
  D_Flip_Flop #(.trigger("falling")) d_ff_2 (
    .clk(Clock), .D(timer_1_ready), .Q(CS2), .reset(Ready));  // open: Qn, preset, en
  D_Flip_Flop #(.trigger("falling")) d_ff_3 (.clk(Clock), .D(CS2), .Q(Ready));  // open: Qn, preset, en, reset
  or or_2 (Chip_Select, CS1, CS2);

  // Other names for the same wires on the sheet: Clck = Clock; CS = Chip_Select; Inst_Out_0[31:0] = output_block_0;
  //   Inst_Out_1[31:0] = output_block_1; Inst_Out_2[31:0] = output_block_2; Inst_Out_3[31:0] = output_block_3;
  //   obtain_inst = Obtain_Instruction; RAM_OUTPUT_0[31:0] = instruction_block_0;
  //   RAM_OUTPUT_1[31:0] = instruction_block_1; RAM_OUTPUT_2[31:0] = instruction_block_2;
  //   RAM_OUTPUT_3[31:0] = instruction_block_3; read_time[3:0] = in_6

  // Notes on the sheet:
  //   Inputs
  //   Outputs
endmodule

module Data_Memory (
  input  [31:0] Address,
  input  [31:0] data_block_0,
  input  [31:0] data_block_1,
  input  [31:0] data_block_2,
  input  [31:0] data_block_3,
  input  [3:0] in_6,
  input  Clock,
  input  Reset,
  input  Obtain_Data,
  output [31:0] output_block_0,
  output [31:0] output_block_1,
  output [31:0] output_block_2,
  output [31:0] output_block_3,
  output WCS,
  output Ready
);

  wire or_1_out, timer_1_ready, WCS1, WCS2;

  D_Flip_Flop #(.trigger("falling")) d_ff_1 (
    .clk(Clock), .D(Obtain_Data), .Q(WCS1), .en(or_1_out));  // open: Qn, preset, reset
  or or_1 (or_1_out, Obtain_Data, timer_1_ready);
  Register #(.width(32)) register_1 (.D(data_block_0), .en(WCS2), .Q(output_block_0), .clk(Clock), .clr(Reset));
  Register #(.width(32)) register_2 (.D(data_block_1), .en(WCS2), .Q(output_block_1), .clk(Clock), .clr(Reset));
  Register #(.width(32)) register_3 (.D(data_block_2), .en(WCS2), .Q(output_block_2), .clk(Clock), .clr(Reset));
  Register #(.width(32)) register_4 (.D(data_block_3), .en(WCS2), .Q(output_block_3), .clk(Clock), .clr(Reset));
  or or_2 (WCS, WCS1, WCS2);
  Timer timer_1 (.Time(in_6), .Start(WCS1), .Ready(timer_1_ready), .Clock(Clock), .Reset(Ready));
  D_Flip_Flop #(.trigger("falling")) d_ff_2 (
    .clk(Clock), .D(timer_1_ready), .Q(WCS2), .reset(Ready));  // open: Qn, preset, en
  D_Flip_Flop #(.trigger("falling")) d_ff_3 (.clk(Clock), .D(WCS2), .Q(Ready));  // open: Qn, preset, en, reset

  // Other names for the same wires on the sheet: Clck = Clock; Inst_Out_0[31:0] = output_block_0;
  //   Inst_Out_1[31:0] = output_block_1; Inst_Out_2[31:0] = output_block_2; Inst_Out_3[31:0] = output_block_3;
  //   RAM_OUTPUT_0[31:0] = data_block_0; RAM_OUTPUT_1[31:0] = data_block_1; RAM_OUTPUT_2[31:0] = data_block_2;
  //   RAM_OUTPUT_3[31:0] = data_block_3; Ready_Write = Ready; write_time[3:0] = in_6

  // Notes on the sheet:
  //   Inputs
  //   Outputs
endmodule

module Timer (
  input  [3:0] Time,
  input  Start,
  input  Clock,
  input  Reset,
  output Ready
);

  wire [3:0] counter_1_q;

  Counter #(.width(4), .max('hf)) counter_1 (
    .count(Start), .Q(counter_1_q), .clk(Clock), .clr(Reset));  // open: load, D, carry
  Comparator #(.width(4)) comparator_1 (.a(Time), .b(counter_1_q), .eq(Ready));  // open: gt, lt
endmodule

// AS
module Address_Separator (
  input  [31:0] Address,
  output [1:0] Output_Selector,
  output [3:0] Mask,
  output [15:0] RAM_Address
);

  Demultiplexer #(.select(2), .enable("false")) demultiplexer_1 (
    .out0(Mask[0]), .out1(Mask[1]), .out2(Mask[2]), .out3(Mask[3]), .in(1'b1), .sel(Address[3:2]));

  assign Output_Selector = Address[3:2];
  assign RAM_Address = Address[19:4];
endmodule

module Branch_Operation (
  input  [31:0] Rs,
  input  [31:0] Rt,
  input  [2:0] Code,
  output [1:0] j
);

  wire beq, bgtz, blez, bltz, bne, Branch_Selector_flag_condition, comparator_2_eq, decoder_1_out0,
       decoder_1_out1, decoder_1_out2, decoder_1_out3, decoder_1_out4, j_t, jr;

  Decoder #(.select(3), .enable("false")) decoder_1 (
    .out0(decoder_1_out0), .out1(decoder_1_out1), .out2(decoder_1_out2), .out3(decoder_1_out3),
    .out4(decoder_1_out4), .out5(j_t), .out6(jr), .sel(Code));  // open: out7
  Branch_Selector Branch_Selector (
    .Op_beq(decoder_1_out0), .Cond_beq(beq), .Op_bne(decoder_1_out1), .Cond_bne(bne),
    .Op_blez(decoder_1_out2), .Cond_blez(blez), .Op_bgtz(decoder_1_out3), .Cond_bgtz(bgtz),
    .Op_bltz(decoder_1_out4), .Cond_bltz(bltz), .Flag_Condition(Branch_Selector_flag_condition));
  or or_1 (j[0], Branch_Selector_flag_condition, jr);
  or or_2 (j[1], jr, j_t);
  Comparator #(.width(32)) comparator_1 (.a(Rs), .b(Rt), .eq(beq));  // open: gt, lt
  not not_1 (bne, beq);
  Comparator #(.width(32)) comparator_2 (.a(Rs), .b({32{1'b0}}), .gt(bgtz), .eq(comparator_2_eq), .lt(bltz));
  or or_3 (blez, comparator_2_eq, bltz);
endmodule

module Branch_Selector (
  input  Op_beq,
  input  Cond_beq,
  input  Op_bne,
  input  Cond_bne,
  input  Op_blez,
  input  Cond_blez,
  input  Op_bgtz,
  input  Cond_bgtz,
  input  Op_bltz,
  input  Cond_bltz,
  output Flag_Condition
);

  wire and_1_out, and_2_out, and_3_out, and_4_out, and_5_out;

  and and_1 (and_1_out, Op_beq, Cond_beq);
  and and_2 (and_2_out, Op_bne, Cond_bne);
  and and_3 (and_3_out, Op_blez, Cond_blez);
  and and_4 (and_4_out, Op_bgtz, Cond_bgtz);
  and and_5 (and_5_out, Op_bltz, Cond_bltz);
  or or_1 (Flag_Condition, and_1_out, and_2_out, and_3_out, and_4_out, and_5_out);
endmodule

module Branch_Control (
  input  in_1,
  input  [31:0] in_2,
  input  [31:0] in_3,
  input  [31:0] in_4,
  input  [25:0] in_5,
  input  [2:0] in_6,
  input  [31:0] in_7,
  output [31:0] IA_prime
);

  wire [1:0] j;
  wire [31:0] adder_1_out, adder_2_out, multiplier_1_out;

  Adder #(.width(32)) adder_1 (.a(in_4), .b(32'h4), .out(adder_1_out));  // open: cin, cout
  Multiplier #(.width(32)) multiplier_1 (.a(in_7), .b(32'h4), .out(multiplier_1_out));  // open: cin, cout
  Branch_Operation Branch_Operation (.Rs(in_2), .Rt(in_3), .Code(in_6), .j(j));
  Adder #(.width(32)) adder_2 (.a(adder_1_out), .b(multiplier_1_out), .out(adder_2_out));  // open: cin, cout
  Multiplexer #(.select(2), .width(32)) multiplexer_1 (
    .in0(adder_1_out), .in1(adder_2_out), .in2({in_4[31:28], in_5, 2'b00}), .in3(in_2), .out(IA_prime),
    .sel(j));  // open: en
  // Probe on j

  // Other names for the same wires on the sheet: Destino_Salto[25:0] = in_5; IA[31:0] = in_4; A[31:0] = in_2;
  //   B[31:0] = in_3; Constant[31:0] = in_7; jmp = in_1; Sb[2:0] = in_6
endmodule

module Program_Counter (
  input  [31:0] IA_prime,
  input  Clock,
  input  Enable,
  input  Reset,
  output [31:0] PC
);

  Register #(.width(32)) register_1 (.D(IA_prime), .en(Enable), .Q(PC), .clk(Clock), .clr(Reset));

  // Other names for the same wires on the sheet: Clck = Clock; Clr = Reset; En = Enable
endmodule

module Control_Unit (
  input  Inputs,
  input  in_2,
  input  in_3,
  input  in_4,
  input  in_5,
  input  in_6,
  input  Instrucciones,
  input  in_8,
  input  in_9,
  input  in_10,
  input  in_11,
  input  in_12,
  input  in_13,
  output Read_Inst,
  output Read_Data,
  output Write,
  output Output,
  output En_Get_Inst,
  output EN_tty,
  output EN_kbd,
  output stop,
  output RW
);

  wire branch, d_ff_1_q, d_ff_3_q, d_ff_4_q, d_ff_5_q, demultiplexer_1_out0, demultiplexer_1_out1, or_4_out,
       RF;
  wire [2:0] or_3_out;

  Demultiplexer #(.select(3), .enable("false")) demultiplexer_1 (
    .out0(demultiplexer_1_out0), .out1(demultiplexer_1_out1), .out2(branch), .out3(RF), .out4(Read_Data),
    .out5(Write), .in(d_ff_1_q), .sel(or_3_out));  // open: out6, out7
  D_Flip_Flop #(.trigger("falling")) d_ff_1 (.clk(Inputs), .D(in_4), .Q(d_ff_1_q));  // open: Qn, preset, en, reset
  or or_1 (or_3_out[2], in_9, in_11);
  or or_2 (or_3_out[1], in_8, in_10);
  or or_3 (or_3_out[0], in_8, Instrucciones, in_11);
  and and_1 (EN_tty, EN_kbd, in_12);
  or or_4 (or_4_out, stop, demultiplexer_1_out0);
  D_Flip_Flop #(.trigger("falling")) d_ff_2 (
    .clk(Inputs), .D(or_4_out), .Q(stop), .reset(in_13));  // open: Qn, preset, en
  D_Flip_Flop #(.trigger("falling")) d_ff_3 (
    .clk(Inputs), .D(demultiplexer_1_out1), .Q(d_ff_3_q), .reset(in_13));  // open: Qn, preset, en
  or or_5 (RW, d_ff_3_q, in_6, RF);
  D_Flip_Flop #(.trigger("falling")) d_ff_4 (
    .clk(Inputs), .D(in_2), .Q(d_ff_4_q), .reset(in_13));  // open: Qn, preset, en
  D_Flip_Flop #(.trigger("falling")) d_ff_5 (
    .clk(Inputs), .D(Output), .Q(d_ff_5_q), .reset(in_13));  // open: Qn, preset, en
  D_Flip_Flop #(.trigger("falling")) d_ff_6 (.clk(Inputs), .D(RW), .Q(EN_kbd));  // open: Qn, preset, en, reset
  or or_6 (Read_Inst, d_ff_4_q, d_ff_5_q);
  or or_7 (Output, EN_kbd, in_5, branch);

  assign En_Get_Inst = in_4;

  // Other names for the same wires on the sheet: ALU = Instrucciones; Cl = Inputs; Cs = in_3; Data = in_6;
  //   En_PC = Output; Get_Inst = in_2; jmp = in_10; mem = in_9; R = in_8; RData = Read_Data; Read = Read_Inst;
  //   Readed = in_4; reset = in_13; tty = in_12; tty_ = EN_kbd; write_inst = in_11; Writen = in_5

  // Notes on the sheet:
  //   Outputs
endmodule

module Instruction_Register (
  input  [31:0] Instruction,
  input  Clock,
  input  Reset,
  input  Enable,
  output [31:0] Output,
  output Instruction_Charged
);

  wire comparator_1_eq, comparator_2_eq;

  Register #(.width(32)) register_1 (.D(Instruction), .en(Enable), .Q(Output), .clk(Clock), .clr(Reset));
  Comparator #(.width(32)) comparator_1 (.a(Output), .b(Instruction), .eq(comparator_1_eq));  // open: gt, lt
  Comparator #(.width(32)) comparator_2 (.a(Instruction), .b({32{1'b0}}), .eq(comparator_2_eq));  // open: gt, lt
  and and_1 (Instruction_Charged, comparator_1_eq, ~comparator_2_eq);  // AND_Gate
endmodule

module Memorie_Address (
  input  [31:0] PC,
  input  [31:0] ALU,
  input  [31:0] SP,
  input  lw,
  input  sw,
  input  pop,
  input  push,
  input  pc_2,
  output [31:0] Memorie_Address
);

  wire [1:0] or_2_out;
  wire [31:0] multiplexer_1_out, subtractor_1_out;

  Multiplexer #(.width(32), .enable("false")) multiplexer_1 (
    .in0(SP), .in1(subtractor_1_out), .out(multiplexer_1_out), .sel(push));
  Subtractor #(.width(32)) subtractor_1 (.a(SP), .b(32'h4), .out(subtractor_1_out));  // open: bin, bout
  or or_1 (or_2_out[1], pop, pc_2, push);
  Multiplexer #(.select(2), .width(32), .enable("false")) multiplexer_2 (
    .in0(PC), .in1(ALU), .in2(multiplexer_1_out), .in3(PC), .out(Memorie_Address), .sel(or_2_out));
  or or_2 (or_2_out[0], lw, pc_2, sw);

  // Other names for the same wires on the sheet: isPC = pc_2
endmodule

module Instruction_Cache (
  input  [31:0] Data_from_RAM_0,
  input  [31:0] Data_from_RAM_2,
  input  [31:0] Data_from_RAM_1,
  input  [31:0] Data_from_RAM_3,
  input  [31:0] Address,
  input  Read,
  input  Clock,
  input  Clear,
  input  RAM_read_finish,
  input  RAM_Write,
  output [31:0] Data_Out_of_Cache,
  output Miss_Hit
);

  wire and_9_out, and_10_out, and_11_out, and_12_out, and_13_out, and_14_out, and_15_out, and_16_out,
       and_17_out, and_18_out, and_19_out, and_20_out, and_21_out, and_22_out, and_23_out, and_24_out,
       and_33_out, and_34_out, and_35_out, and_36_out, and_37_out, and_38_out, and_39_out, and_40_out,
       and_41_out, and_42_out, and_43_out, and_44_out, and_45_out, and_46_out, and_47_out, and_48_out, ClV0,
       ClV1, ClV2, ClV3, ClV4, ClV5, ClV6, ClV7, ClV8, ClV9, ClV10, ClV11, ClV12, ClV13, ClV14, ClV15, E0,
       E1, E2, E3, E4, E5, E6, E7, E8, E9, E10, E11, E12, E13, E14, E15, Line_0, Line_1, Line_2, Line_3,
       Line_4, Line_5, Line_6, Line_7, Line_8, Line_9, Line_10, Line_11, Line_12, Line_13, Line_14, Line_15,
       Match_Data0, Match_Data1, Match_Data2, Match_Data3, Match_Data4, Match_Data5, Match_Data6,
       Match_Data7, Match_Data8, Match_Data9, Match_Data10, Match_Data11, Match_Data12, Match_Data13,
       Match_Data14, Match_Data15, Match_Tag0, Match_Tag1, Match_Tag2, Match_Tag3, Match_Tag4, Match_Tag5,
       Match_Tag6, Match_Tag7, Match_Tag8, Match_Tag9, Match_Tag10, Match_Tag11, Match_Tag12, Match_Tag13,
       Match_Tag14, Match_Tag15, or_17_out, V0, V1, V2, V3, V4, V5, V6, V7, V8, V9, V10, V11, V12, V13, V14,
       V15;
  wire [25:0] Tag, Tag0, Tag1, Tag2, Tag3, Tag4, Tag5, Tag6, Tag7, Tag8, Tag9, Tag10, Tag11, Tag12, Tag13,
       Tag15;
  wire [31:0] _000000, _000001, _000010, _000011, _000100, _000101, _000110, _000111, _001000, _001001,
       _001010, _001011, _001100, _001101, _001110, _001111, _010000, _010001, _010010, _010011, _010100,
       _010101, _010110, _010111, _011000, _011001, _011010, _011011, _011100, _011101, _011110, _011111,
       _100000, _100001, _100010, _100011, _100100, _100101, _100110, _100111, _101000, _101001, _101010,
       _101011, _101100, _101101, _101110, _101111, _110000, _110001, _110010, _110011, _110100, _110101,
       _110110, _110111, _111000, _111001, _111010, _111011, _111100, _111101, _111110, _111111, Out_00,
       Out_01, Out_10, Out_11;

  and and_1 (Match_Data0, Match_Tag0, Line_0);
  and and_2 (Match_Data1, Match_Tag1, Line_1);
  and and_3 (Match_Data2, Match_Tag2, Line_2);
  and and_4 (Match_Data3, Match_Tag3, Line_3);
  and and_5 (Match_Data4, Match_Tag4, Line_4);
  and and_6 (Match_Data5, Match_Tag5, Line_5);
  and and_7 (Match_Data6, Match_Tag6, Line_6);
  and and_8 (Match_Data7, Match_Tag7, Line_7);
  assign Tag = {{2{Address[31]}}, Address[31:8]};  // Bit_Extender bit_extender_1
  and and_9 (and_9_out, Match_Data0, RAM_Write);
  and and_10 (and_10_out, Match_Data1, RAM_Write);
  and and_11 (and_11_out, Match_Data2, RAM_Write);
  and and_12 (and_12_out, Match_Data3, RAM_Write);
  and and_13 (and_13_out, Match_Data4, RAM_Write);
  and and_14 (and_14_out, Match_Data5, RAM_Write);
  and and_15 (and_15_out, Match_Data6, RAM_Write);
  and and_16 (and_16_out, Match_Data7, RAM_Write);
  and and_17 (and_17_out, Match_Data8, RAM_Write);
  and and_18 (and_18_out, Match_Data9, RAM_Write);
  and and_19 (and_19_out, Match_Data10, RAM_Write);
  and and_20 (and_20_out, Match_Data11, RAM_Write);
  and and_21 (and_21_out, Match_Data12, RAM_Write);
  and and_22 (and_22_out, Match_Data13, RAM_Write);
  and and_23 (and_23_out, Match_Data14, RAM_Write);
  and and_24 (and_24_out, Match_Data15, RAM_Write);
  and and_25 (Match_Data8, Match_Tag8, Line_8);
  and and_26 (Match_Data9, Match_Tag9, Line_9);
  and and_27 (Match_Data10, Match_Tag10, Line_10);
  and and_28 (Match_Data11, Match_Tag11, Line_11);
  and and_29 (Match_Data12, Match_Tag12, Line_12);
  and and_30 (Match_Data13, Match_Tag13, Line_13);
  and and_31 (Match_Data14, Match_Tag14, Line_14);
  and and_32 (Match_Data15, Match_Tag15, Line_15);
  or or_1 (ClV0, Clear, and_9_out);
  or or_2 (ClV1, Clear, and_10_out);
  or or_3 (ClV2, Clear, and_11_out);
  or or_4 (ClV3, Clear, and_12_out);
  or or_5 (ClV4, Clear, and_13_out);
  or or_6 (ClV5, Clear, and_14_out);
  or or_7 (ClV6, Clear, and_15_out);
  or or_8 (ClV7, Clear, and_16_out);
  or or_9 (ClV8, Clear, and_17_out);
  or or_10 (ClV9, Clear, and_18_out);
  or or_11 (ClV10, Clear, and_19_out);
  or or_12 (ClV11, Clear, and_20_out);
  or or_13 (ClV12, Clear, and_21_out);
  or or_14 (ClV13, Clear, and_22_out);
  or or_15 (ClV14, Clear, and_23_out);
  or or_16 (ClV15, Clear, and_24_out);
  Comparator #(.width(26)) comparator_1 (.a(Tag), .b(Tag0), .eq(Match_Tag0));  // open: gt, lt
  Comparator #(.width(26)) comparator_2 (.a(Tag), .b(Tag1), .eq(Match_Tag1));  // open: gt, lt
  Comparator #(.width(26)) comparator_3 (.a(Tag), .b(Tag2), .eq(Match_Tag2));  // open: gt, lt
  Comparator #(.width(26)) comparator_4 (.a(Tag), .b(Tag3), .eq(Match_Tag3));  // open: gt, lt
  Comparator #(.width(26)) comparator_5 (.a(Tag), .b(Tag4), .eq(Match_Tag4));  // open: gt, lt
  Comparator #(.width(26)) comparator_6 (.a(Tag), .b(Tag5), .eq(Match_Tag5));  // open: gt, lt
  Comparator #(.width(26)) comparator_7 (.a(Tag), .b(Tag6), .eq(Match_Tag6));  // open: gt, lt
  Comparator #(.width(26)) comparator_8 (.a(Tag), .b(Tag7), .eq(Match_Tag7));  // open: gt, lt
  Comparator #(.width(26)) comparator_9 (.a(Tag), .b(Tag8), .eq(Match_Tag8));  // open: gt, lt
  Comparator #(.width(26)) comparator_10 (.a(Tag), .b(Tag9), .eq(Match_Tag9));  // open: gt, lt
  Comparator #(.width(26)) comparator_11 (.a(Tag), .b(Tag10), .eq(Match_Tag10));  // open: gt, lt
  Comparator #(.width(26)) comparator_12 (.a(Tag), .b(Tag11), .eq(Match_Tag11));  // open: gt, lt
  Comparator #(.width(26)) comparator_13 (.a(Tag), .b(Tag12), .eq(Match_Tag12));  // open: gt, lt
  Comparator #(.width(26)) comparator_14 (.a(Tag), .b(Tag13), .eq(Match_Tag13));  // open: gt, lt
  Comparator #(.width(26)) comparator_15 (.a(Tag), .b(Tag), .eq(Match_Tag14));  // open: gt, lt
  Comparator #(.width(26)) comparator_16 (.a(Tag), .b(Tag15), .eq(Match_Tag15));  // open: gt, lt
  Decoder #(.select(4), .enable("false")) decoder_1 (
    .out0(Line_0), .out1(Line_1), .out2(Line_2), .out3(Line_3), .out4(Line_4), .out5(Line_5), .out6(Line_6),
    .out7(Line_7), .out8(Line_8), .out9(Line_9), .out10(Line_10), .out11(Line_11), .out12(Line_12),
    .out13(Line_13), .out14(Line_14), .out15(Line_15), .sel(Address[7:4]));
  and and_33 (and_33_out, Match_Data0, V0);
  and and_34 (and_34_out, Match_Data8, V8);
  and and_35 (and_35_out, Match_Data1, V1);
  and and_36 (and_36_out, Match_Data9, V9);
  and and_37 (and_37_out, Match_Data2, V2);
  and and_38 (and_38_out, Match_Data10, V10);
  and and_39 (and_39_out, Match_Data3, V3);
  and and_40 (and_40_out, Match_Data11, V11);
  and and_41 (and_41_out, Match_Data4, V4);
  and and_42 (and_42_out, Match_Data12, V12);
  and and_43 (and_43_out, Match_Data5, V5);
  and and_44 (and_44_out, Match_Data13, V13);
  and and_45 (and_45_out, Match_Data6, V6);
  and and_46 (and_46_out, Match_Data14, V14);
  and and_47 (and_47_out, Match_Data7, V7);
  and and_48 (and_48_out, Match_Data15, V15);
  Register #(.width(26)) u_Tag0 (.D(Tag), .en(E0), .Q(Tag0), .clk(Clear), .clr(Clear));
  Register #(.width(26)) u_Tag1 (.D(Tag), .en(E1), .Q(Tag1), .clk(Clear), .clr(Clear));
  Register #(.width(26)) u_Tag2 (.D(Tag), .en(E2), .Q(Tag2), .clk(Clear), .clr(Clear));
  Register #(.width(26)) u_Tag3 (.D(Tag), .en(E3), .Q(Tag3), .clk(Clear), .clr(Clear));
  Register #(.width(26)) u_Tag4 (.D(Tag), .en(E4), .Q(Tag4), .clk(Clear), .clr(Clear));
  Register #(.width(26)) u_Tag5 (.D(Tag), .en(E5), .Q(Tag5), .clk(Clear), .clr(Clear));
  Register #(.width(26)) u_Tag6 (.D(Tag), .en(E6), .Q(Tag6), .clk(Clear), .clr(Clear));
  Register #(.width(26)) u_Tag7 (.D(Tag), .en(E7), .Q(Tag7), .clk(Clear), .clr(Clear));
  or or_17 (or_17_out, and_33_out, and_34_out, and_35_out, and_36_out, and_37_out, and_38_out, and_39_out, and_40_out, and_41_out, and_42_out, and_43_out, and_44_out, and_45_out, and_46_out, and_47_out, and_48_out);
  and and_49 (Miss_Hit, or_17_out, Read);
  Register #(.width(26)) u_Tag8 (.D(Tag), .en(E8), .Q(Tag8), .clk(Clear), .clr(Clear));
  Register #(.width(26)) u_Tag9 (.D(Tag), .en(E9), .Q(Tag9), .clk(Clear), .clr(Clear));
  Register #(.width(26)) u_Tag10 (.D(Tag), .en(E10), .Q(Tag10), .clk(Clear), .clr(Clear));
  Register #(.width(26)) u_Tag11 (.D(Tag), .en(E11), .Q(Tag11), .clk(Clear), .clr(Clear));
  Register #(.width(26)) u_Tag12 (.D(Tag), .en(E12), .Q(Tag12), .clk(Clear), .clr(Clear));
  Register #(.width(26)) u_Tag13 (.D(Tag), .en(E13), .Q(Tag13), .clk(Clear), .clr(Clear));
  Register #(.width(26)) Tag14 (.D(Tag), .en(E14), .Q(Tag), .clk(Clear), .clr(Clear));
  Register #(.width(26)) u_Tag15 (.D(Tag), .en(E15), .Q(Tag15), .clk(Clear), .clr(Clear));
  Bit_de_validez bit_de_validez_1 (.Clock(Clear), .In(E0), .Clear(ClV0), .Output(V0));
  Bit_de_validez bit_de_validez_2 (.Clock(Clear), .In(E1), .Clear(ClV1), .Output(V1));
  Bit_de_validez bit_de_validez_3 (.Clock(Clear), .In(E2), .Clear(ClV2), .Output(V2));
  Bit_de_validez bit_de_validez_4 (.Clock(Clear), .In(E3), .Clear(ClV3), .Output(V3));
  Bit_de_validez bit_de_validez_5 (.Clock(Clear), .In(E4), .Clear(ClV4), .Output(V4));
  Bit_de_validez bit_de_validez_6 (.Clock(Clear), .In(E5), .Clear(ClV5), .Output(V5));
  Bit_de_validez bit_de_validez_7 (.Clock(Clear), .In(E6), .Clear(ClV6), .Output(V6));
  Bit_de_validez bit_de_validez_8 (.Clock(Clear), .In(E7), .Clear(ClV7), .Output(V7));
  Bit_de_validez bit_de_validez_9 (.Clock(Clear), .In(E8), .Clear(ClV8), .Output(V8));
  Bit_de_validez bit_de_validez_10 (.Clock(Clear), .In(E9), .Clear(ClV9), .Output(V9));
  Bit_de_validez bit_de_validez_11 (.Clock(Clear), .In(E10), .Clear(ClV10), .Output(V10));
  Bit_de_validez bit_de_validez_12 (.Clock(Clear), .In(E11), .Clear(ClV11), .Output(V11));
  Bit_de_validez bit_de_validez_13 (.Clock(Clear), .In(E12), .Clear(ClV12), .Output(V12));
  Bit_de_validez bit_de_validez_14 (.Clock(Clear), .In(E13), .Clear(ClV13), .Output(V13));
  Bit_de_validez bit_de_validez_15 (.Clock(Clear), .In(E14), .Clear(ClV14), .Output(V14));
  Bit_de_validez bit_de_validez_16 (.Clock(Clear), .In(E15), .Clear(ClV15), .Output(V15));
  Register #(.width(32)) register_1 (.D(Data_from_RAM_3), .en(E0), .Q(_000011), .clk(Clear), .clr(Clear));
  Register #(.width(32)) register_2 (.D(Data_from_RAM_3), .en(E1), .Q(_000111), .clk(Clear), .clr(Clear));
  Register #(.width(32)) register_3 (.D(Data_from_RAM_3), .en(E2), .Q(_001011), .clk(Clear), .clr(Clear));
  Register #(.width(32)) register_4 (.D(Data_from_RAM_3), .en(E3), .Q(_001111), .clk(Clear), .clr(Clear));
  Register #(.width(32)) register_5 (.D(Data_from_RAM_3), .en(E4), .Q(_010011), .clk(Clear), .clr(Clear));
  Register #(.width(32)) register_6 (.D(Data_from_RAM_3), .en(E5), .Q(_010111));  // open: clk, clr
  Register #(.width(32)) register_7 (.D(Data_from_RAM_3), .en(E6), .Q(_011011), .clk(Clear), .clr(Clear));
  Register #(.width(32)) register_8 (.D(Data_from_RAM_3), .en(E7), .Q(_011111), .clk(Clear), .clr(Clear));
  Register #(.width(32)) register_9 (.D(Data_from_RAM_3), .en(E8), .Q(_100011), .clk(Clear), .clr(Clear));
  Register #(.width(32)) register_10 (.D(Data_from_RAM_3), .en(E9), .Q(_100111), .clk(Clear), .clr(Clear));
  Register #(.width(32)) register_11 (.D(Data_from_RAM_3), .en(E10), .Q(_101011), .clk(Clear), .clr(Clear));
  Register #(.width(32)) register_12 (.D(Data_from_RAM_3), .en(E11), .Q(_101111), .clk(Clear), .clr(Clear));
  Register #(.width(32)) register_13 (.D(Data_from_RAM_3), .en(E12), .Q(_110011), .clk(Clear), .clr(Clear));
  Register #(.width(32)) register_14 (.D(Data_from_RAM_3), .en(E13), .Q(_110111), .clk(Clear), .clr(Clear));
  Register #(.width(32)) register_15 (.D(Data_from_RAM_3), .en(E14), .Q(_111011), .clk(Clear), .clr(Clear));
  Register #(.width(32)) register_16 (.D(Data_from_RAM_3), .en(E15), .Q(_111111), .clk(Clear), .clr(Clear));
  Multiplexer #(.select(2), .width(32), .enable("false")) multiplexer_1 (
    .in0(Out_00), .in1(Out_01), .in2(Out_10), .in3(Out_11), .out(Data_Out_of_Cache), .sel(Address[3:2]));
  Register #(.width(32)) register_17 (.D(Data_from_RAM_2), .en(E0), .Q(_000010), .clk(Clear), .clr(Clear));
  Register #(.width(32)) register_18 (.D(Data_from_RAM_2), .en(E1), .Q(_000110), .clk(Clear), .clr(Clear));
  Register #(.width(32)) register_19 (.D(Data_from_RAM_2), .en(E2), .Q(_001010), .clk(Clear), .clr(Clear));
  Register #(.width(32)) register_20 (.D(Data_from_RAM_2), .en(E3), .Q(_001110), .clk(Clear), .clr(Clear));
  Register #(.width(32)) register_21 (.D(Data_from_RAM_2), .en(E4), .Q(_010010), .clk(Clear), .clr(Clear));
  Register #(.width(32)) register_22 (.D(Data_from_RAM_2), .en(E5), .Q(_010110));  // open: clk, clr
  Register #(.width(32)) register_23 (.D(Data_from_RAM_2), .en(E6), .Q(_011010), .clk(Clear), .clr(Clear));
  Register #(.width(32)) register_24 (.D(Data_from_RAM_2), .en(E7), .Q(_011110), .clk(Clear), .clr(Clear));
  Register #(.width(32)) register_25 (.D(Data_from_RAM_2), .en(E8), .Q(_100010), .clk(Clear), .clr(Clear));
  Register #(.width(32)) register_26 (.D(Data_from_RAM_2), .en(E9), .Q(_100110), .clk(Clear), .clr(Clear));
  Register #(.width(32)) register_27 (.D(Data_from_RAM_2), .en(E10), .Q(_101010), .clk(Clear), .clr(Clear));
  Register #(.width(32)) register_28 (.D(Data_from_RAM_2), .en(E11), .Q(_101110), .clk(Clear), .clr(Clear));
  Register #(.width(32)) register_29 (.D(Data_from_RAM_2), .en(E12), .Q(_110010), .clk(Clear), .clr(Clear));
  Register #(.width(32)) register_30 (.D(Data_from_RAM_2), .en(E13), .Q(_110110), .clk(Clear), .clr(Clear));
  Register #(.width(32)) register_31 (.D(Data_from_RAM_2), .en(E14), .Q(_111010), .clk(Clear), .clr(Clear));
  Register #(.width(32)) register_32 (.D(Data_from_RAM_2), .en(E15), .Q(_111110), .clk(Clear), .clr(Clear));
  Register #(.width(32)) register_33 (.D(Data_from_RAM_1), .en(E0), .Q(_000001), .clk(Clear), .clr(Clear));
  Register #(.width(32)) register_34 (.D(Data_from_RAM_1), .en(E1), .Q(_000101), .clk(Clear), .clr(Clear));
  Register #(.width(32)) register_35 (.D(Data_from_RAM_1), .en(E2), .Q(_001001), .clk(Clear), .clr(Clear));
  Register #(.width(32)) register_36 (.D(Data_from_RAM_1), .en(E3), .Q(_001101), .clk(Clear), .clr(Clear));
  Register #(.width(32)) register_37 (.D(Data_from_RAM_1), .en(E4), .Q(_010001), .clk(Clear), .clr(Clear));
  Register #(.width(32)) register_38 (.D(Data_from_RAM_1), .en(E5), .Q(_010101));  // open: clk, clr
  Register #(.width(32)) register_39 (.D(Data_from_RAM_1), .en(E6), .Q(_011001), .clk(Clear), .clr(Clear));
  Register #(.width(32)) register_40 (.D(Data_from_RAM_1), .en(E7), .Q(_011101), .clk(Clear), .clr(Clear));
  Register #(.width(32)) register_41 (.D(Data_from_RAM_1), .en(E8), .Q(_100001), .clk(Clear), .clr(Clear));
  Register #(.width(32)) register_42 (.D(Data_from_RAM_1), .en(E9), .Q(_100101), .clk(Clear), .clr(Clear));
  Register #(.width(32)) register_43 (.D(Data_from_RAM_1), .en(E10), .Q(_101001), .clk(Clear), .clr(Clear));
  Register #(.width(32)) register_44 (.D(Data_from_RAM_1), .en(E11), .Q(_101101), .clk(Clear), .clr(Clear));
  Register #(.width(32)) register_45 (.D(Data_from_RAM_1), .en(E12), .Q(_110001), .clk(Clear), .clr(Clear));
  Register #(.width(32)) register_46 (.D(Data_from_RAM_1), .en(E13), .Q(_110101), .clk(Clear), .clr(Clear));
  Register #(.width(32)) register_47 (.D(Data_from_RAM_1), .en(E14), .Q(_111001), .clk(Clear), .clr(Clear));
  Register #(.width(32)) register_48 (.D(Data_from_RAM_1), .en(E15), .Q(_111101), .clk(Clear), .clr(Clear));
  and and_50 (E0, RAM_read_finish, Line_0);
  and and_51 (E1, RAM_read_finish, Line_1);
  and and_52 (E2, RAM_read_finish, Line_2);
  and and_53 (E3, RAM_read_finish, Line_3);
  and and_54 (E4, RAM_read_finish, Line_4);
  and and_55 (E5, RAM_read_finish, Line_5);
  and and_56 (E6, RAM_read_finish, Line_6);
  and and_57 (E7, RAM_read_finish, Line_7);
  Register #(.width(32)) register_49 (.D(Data_from_RAM_0), .en(E0), .Q(_000000), .clk(Clear), .clr(Clear));
  Register #(.width(32)) register_50 (.D(Data_from_RAM_0), .en(E1), .Q(_000100), .clk(Clear), .clr(Clear));
  Register #(.width(32)) register_51 (.D(Data_from_RAM_0), .en(E2), .Q(_001000), .clk(Clear), .clr(Clear));
  Register #(.width(32)) register_52 (.D(Data_from_RAM_0), .en(E3), .Q(_001100), .clk(Clear), .clr(Clear));
  Register #(.width(32)) register_53 (.D(Data_from_RAM_0), .en(E4), .Q(_010000), .clk(Clear), .clr(Clear));
  Register #(.width(32)) register_54 (.D(Data_from_RAM_0), .en(E5), .Q(_010100), .clk(Clear), .clr(Clear));
  Register #(.width(32)) register_55 (.D(Data_from_RAM_0), .en(E6), .Q(_011000), .clk(Clear), .clr(Clear));
  Register #(.width(32)) register_56 (.D(Data_from_RAM_0), .en(E7), .Q(_011100), .clk(Clear), .clr(Clear));
  Register #(.width(32)) register_57 (.D(Data_from_RAM_0), .en(E8), .Q(_100000), .clk(Clear), .clr(Clear));
  Register #(.width(32)) register_58 (.D(Data_from_RAM_0), .en(E9), .Q(_100100), .clk(Clear), .clr(Clear));
  Register #(.width(32)) register_59 (.D(Data_from_RAM_0), .en(E10), .Q(_101000), .clk(Clear), .clr(Clear));
  Register #(.width(32)) register_60 (.D(Data_from_RAM_0), .en(E11), .Q(_101100), .clk(Clear), .clr(Clear));
  Register #(.width(32)) register_61 (.D(Data_from_RAM_0), .en(E12), .Q(_110000), .clk(Clear), .clr(Clear));
  Register #(.width(32)) register_62 (.D(Data_from_RAM_0), .en(E13), .Q(_110100), .clk(Clear), .clr(Clear));
  Register #(.width(32)) register_63 (.D(Data_from_RAM_0), .en(E14), .Q(_111000), .clk(Clear), .clr(Clear));
  Register #(.width(32)) register_64 (.D(Data_from_RAM_0), .en(E15), .Q(_111100), .clk(Clear), .clr(Clear));
  and and_58 (E8, RAM_read_finish, Line_8);
  and and_59 (E9, RAM_read_finish, Line_9);
  and and_60 (E10, RAM_read_finish, Line_10);
  and and_61 (E11, RAM_read_finish, Line_11);
  and and_62 (E12, RAM_read_finish, Line_12);
  and and_63 (E13, RAM_read_finish, Line_13);
  and and_64 (E14, RAM_read_finish, Line_14);
  and and_65 (E15, RAM_read_finish, Line_15);
  Multiplexer #(.select(4), .width(32)) multiplexer_2 (
    .in0(_000000), .in1(_000100), .in2(_001000), .in3(_001100), .in4(_010000), .in5(_010100), .in6(_011000),
    .in7(_011100), .in8(_100000), .in9(_100100), .in10(_101000), .in11(_101100), .in12(_110000),
    .in13(_110100), .in14(_111000), .in15(_111100), .out(Out_00), .sel(Address[7:4]), .en(Miss_Hit));
  Multiplexer #(.select(4), .width(32)) multiplexer_3 (
    .in0(_000001), .in1(_000101), .in2(_001001), .in3(_001101), .in4(_010001), .in5(_010101), .in6(_011001),
    .in7(_011101), .in8(_100001), .in9(_100101), .in10(_101001), .in11(_101101), .in12(_110001),
    .in13(_110101), .in14(_111001), .in15(_111101), .out(Out_01), .sel(Address[7:4]), .en(Miss_Hit));
  Multiplexer #(.select(4), .width(32)) multiplexer_4 (
    .in0(_000010), .in1(_000110), .in2(_001010), .in3(_001110), .in4(_010010), .in5(_010110), .in6(_011010),
    .in7(_011110), .in8(_100010), .in9(_100110), .in10(_101010), .in11(_101110), .in12(_110010),
    .in13(_110110), .in14(_111010), .in15(_111110), .out(Out_10), .sel(Address[7:4]), .en(Miss_Hit));
  Multiplexer #(.select(4), .width(32)) multiplexer_5 (
    .in0(_000011), .in1(_000111), .in2(_001011), .in3(_001111), .in4(_010011), .in5(_010111), .in6(_011011),
    .in7(_011111), .in8(_100011), .in9(_100111), .in10(_101011), .in11(_101111), .in12(_110011),
    .in13(_110111), .in14(_111011), .in15(_111111), .out(Out_11), .sel(Address[7:4]), .en(Miss_Hit));

  assign Clock = Clear;

  // Other names for the same wires on the sheet: Offset[1:0] = Address[3:2]; Index[3:0] = Address[7:4];
  //   Data_to_cpu[31:0] = Data_Out_of_Cache; Hit = Miss_Hit; In_00[31:0] = Data_from_RAM_0;
  //   In_01[31:0] = Data_from_RAM_1; In_10[31:0] = Data_from_RAM_2; In_11[31:0] = Data_from_RAM_3; T0 = E0; T1 = E1;
  //   T2 = E2; T3 = E3; T4 = E4; T5 = E5; T6 = E6; T7 = E7; T8 = E8; T9 = E9; T10 = E10; T11 = E11; T12 = E12;
  //   T13 = E13; T14 = E14; T15 = E15; Tag14[25:0] = Tag

  // Notes on the sheet:
  //   Inputs
endmodule

// Valid
module Bit_de_validez (
  input  Clock,
  input  In,
  input  Clear,
  output Output
);

  wire and_1_out, d_ff_1_qn;

  and and_1 (and_1_out, In, d_ff_1_qn);
  D_Flip_Flop #(.trigger("falling")) d_ff_1 (
    .clk(Clock), .D(and_1_out), .Q(Output), .Qn(d_ff_1_qn), .en(d_ff_1_qn), .reset(Clear));  // open: preset
endmodule

module Inversor (
  input  [31:0] Data_In,
  output [31:0] Data_Out
);


  assign Data_Out = {Data_In[7:0], Data_In[15:8], Data_In[23:16], Data_In[31:24]};
endmodule

module Instruction_Memory__Cache (
  input  Clock,
  input  Reset,
  input  Get,
  input  [31:0] Address,
  input  [3:0] Read_Time,
  input  [31:0] RO0,
  input  [31:0] RO2,
  input  [31:0] RO1,
  input  [31:0] RO3,
  input  Write_RAM,
  input  Halt,
  output Chip_Select,
  output Ready,
  output [15:0] RAM_Address,
  output Cache_on_work,
  output [31:0] Data_output
);

  wire CS1, CS2, d_ff_3_q, Miss_Hit, nStop, or_2_out, or_3_out, or_4_out, or_5_out, out_sec, RAM_read_finish,
       Reset_t, Stop, timer_1_ready;
  wire [1:0] Output_Selector;
  wire [3:0] Mask;
  wire [31:0] Data_from_Cache, Hits_q, instruction_cache_1_data_out_of_cache, Inversor_2_data_out,
       Inversor_3_data_out, Inversor_4_data_out, Inversor_5_data_out, Inversor_data_out, Misses_q,
       multiplexer_1_out, RAM_OUTPUT_0, RAM_OUTPUT_1, RAM_OUTPUT_2, RAM_OUTPUT_3;

  or or_1 (Reset_t, RAM_read_finish, Reset);
  Register #(.width(32)) register_1 (.D(RO0), .en(CS2), .Q(RAM_OUTPUT_0), .clk(Clock));  // open: clr
  Register #(.width(32)) register_2 (.D(RO1), .en(CS2), .Q(RAM_OUTPUT_1), .clk(Clock));  // open: clr
  Address_Separator address_separator_1 (
    .Address(Address), .Mask(Mask), .RAM_Address(RAM_Address), .Output_Selector(Output_Selector));
  Inversor Inversor (.Data_In(RAM_OUTPUT_2), .Data_Out(Inversor_data_out));
  Inversor Inversor_2 (.Data_In(RAM_OUTPUT_1), .Data_Out(Inversor_2_data_out));
  Inversor Inversor_3 (.Data_In(RAM_OUTPUT_0), .Data_Out(Inversor_3_data_out));
  Register #(.width(32)) register_3 (.D(RO2), .en(CS2), .Q(RAM_OUTPUT_2), .clk(Clock));  // open: clr
  Register #(.width(32)) register_4 (.D(RO3), .en(CS2), .Q(RAM_OUTPUT_3), .clk(Clock));  // open: clr
  Inversor Inversor_4 (.Data_In(RAM_OUTPUT_3), .Data_Out(Inversor_4_data_out));
  or or_2 (or_2_out, Get, timer_1_ready);
  Register #(.width(32), .trigger("high")) register_5 (
    .D(instruction_cache_1_data_out_of_cache), .en(Miss_Hit), .Q(Data_from_Cache), .clk(Clock));  // open: clr
  Instruction_Cache instruction_cache_1 (
    .Data_from_RAM_0(Inversor_3_data_out), .Data_from_RAM_2(Inversor_data_out),
    .Data_from_RAM_1(Inversor_2_data_out), .Data_from_RAM_3(Inversor_4_data_out), .Address(Address),
    .Read(Get), .Clock(Clock), .Clear(Reset), .RAM_read_finish(RAM_read_finish), .RAM_Write(Write_RAM),
    .Data_Out_of_Cache(instruction_cache_1_data_out_of_cache), .Miss_Hit(Miss_Hit));
  or or_3 (or_3_out, CS1, CS2);
  D_Flip_Flop #(.trigger("falling")) d_ff_1 (
    .clk(Clock), .D(Get), .Q(CS1), .en(or_2_out), .reset(Miss_Hit));  // open: Qn, preset
  and and_1 (Chip_Select, or_3_out, nStop);
  // Probe on Data_from_Cache
  Timer timer_1 (.Time(Read_Time), .Start(CS1), .Ready(timer_1_ready), .Clock(Clock), .Reset(Reset_t));
  D_Flip_Flop #(.trigger("falling")) d_ff_2 (
    .clk(Clock), .D(timer_1_ready), .Q(CS2), .reset(d_ff_3_q));  // open: Qn, preset, en
  Inversor Inversor_5 (.Data_In(multiplexer_1_out), .Data_Out(Inversor_5_data_out));
  Multiplexer #(.select(2), .width(32), .disabled(0), .enable("false")) multiplexer_1 (
    .in0(RAM_OUTPUT_0), .in1(RAM_OUTPUT_1), .in2(RAM_OUTPUT_2), .in3(RAM_OUTPUT_3), .out(multiplexer_1_out),
    .sel(Output_Selector));
  // Probe on Output_Selector
  and and_2 (Ready, nStop, or_4_out);
  or or_4 (or_4_out, out_sec, d_ff_3_q);
  D_Flip_Flop #(.trigger("falling")) d_ff_3 (.clk(Clock), .D(CS2), .Q(d_ff_3_q));  // open: Qn, preset, en, reset
  Multiplexer #(.width(32), .disabled(0), .enable("false")) multiplexer_2 (
    .in0(Inversor_5_data_out), .in1(Data_from_Cache), .out(Data_output), .sel(out_sec));
  D_Flip_Flop #(.trigger("falling")) d_ff_4 (
    .clk(Clock), .D(Miss_Hit), .Q(Cache_on_work));  // open: Qn, preset, en, reset
  and and_3 (RAM_read_finish, ~Miss_Hit, d_ff_3_q);  // AND_Gate
  Counter #(.width(32), .max('hffffffff)) Misses (
    .load(Stop), .D(Misses_q), .count(nStop), .Q(Misses_q), .clk(d_ff_3_q));  // open: carry, clr
  // Probe on Misses_q
  D_Flip_Flop #(.trigger("falling")) d_ff_5 (
    .clk(Clock), .D(Cache_on_work), .Q(out_sec));  // open: Qn, preset, en, reset
  or or_5 (or_5_out, Stop, Halt);
  Counter #(.width(32), .max('hffffffff)) Hits (
    .load(Stop), .D(Hits_q), .count(nStop), .Q(Hits_q), .clk(out_sec));  // open: carry, clr
  D_Flip_Flop #(.trigger("falling")) d_ff_6 (
    .clk(Clock), .D(or_5_out), .Q(Stop), .Qn(nStop));  // open: preset, en, reset
  // Probe on Hits_q

  // Other names for the same wires on the sheet: Addr[31:0] = Address; Clck = Clock; Clr = Reset

  // Notes on the sheet:
  //   Instruction Cache
endmodule

// Control Unit
module control_unit_cache (
  input  Clock,
  input  IMR,
  input  DMR,
  input  II,
  input  Chip_Select,
  input  Write_Register,
  input  Cache_Working,
  output Enable
);

  wire d_ff_1_q, d_ff_2_qn, or_1_out, or_2_out, starter_1_start;

  D_Flip_Flop #(.trigger("falling")) d_ff_1 (
    .clk(Clock), .D(Write_Register), .Q(d_ff_1_q));  // open: Qn, preset, en, reset
  Starter starter_1 (.Clock(Clock), .Start(starter_1_start));
  or or_1 (or_1_out, DMR, d_ff_1_q, II);
  or or_2 (or_2_out, or_1_out, starter_1_start);
  D_Flip_Flop #(.trigger("falling")) d_ff_2 (.clk(Clock), .D(Enable), .Qn(d_ff_2_qn));  // open: Q, preset, en, reset
  and and_1 (Enable, d_ff_2_qn, ~Chip_Select, ~IMR, or_2_out, ~Cache_Working);  // AND_Gate

  // Other names for the same wires on the sheet: CS = Chip_Select
endmodule

// starter
module Starter (
  input  Clock,
  output Start
);

  wire d_ff_1_q, d_ff_1_qn;

  D_Flip_Flop #(.trigger("falling")) d_ff_1 (
    .clk(Clock), .D(d_ff_1_qn), .Q(d_ff_1_q), .Qn(d_ff_1_qn), .en(d_ff_1_qn));  // open: preset, reset
  D_Flip_Flop d_ff_2 (.clk(Clock), .D(d_ff_1_q), .Qn(Start), .en(Start));  // open: Q, preset, reset
endmodule
